# Fritzing sketch LabAnalogInPhotoTransistorNano (saved by Fritzing 0.9.3b)
breadboards: 1

parts:
  Part1 = Arduino Nano (Rev3.0)
  Q1 = LTR-301 [package=ltr-301]
  R1 = Resistor [tolerance=±5% resistance=10k package=THT]

nets:
  N1: Part1.GND, R1.Pin_0
  N2: Part1.A0, Q1.C, R1.Pin_1
  N3: Part1.3V3, Q1.E
