# Fritzing sketch LabAnalogInNano (saved by Fritzing 0.9.3b)
breadboards: 1

parts:
  U1 = POT [package=alps_pot]
  LED1 = LED - 5mm [color="Red (633nm)" package="5 mm [THT]"]
  R1 = Resistor [tolerance=±5% resistance=220 package=THT]
  Part1 = Arduino Nano (Rev3.0)

nets:
  N1: U1.E, Part1.3V3
  N2: U1.S, Part1.A0
  GND: U1.A, LED1.cathode, Part1.GND
  N3: LED1.anode, R1.Pin_1
  N4: R1.Pin_0, Part1.D9
