# Fritzing sketch Nano_NeoPixel (saved by Fritzing 0.9.9b)
breadboards: 1

parts:
  Part3 = Arduino Nano 33 IoT
  NEOPIXEL1 = Neopixel Strip -- White (60/m) [part_number=1138]
  IC1 = Voltage Regulator [package=to220-igo]
  JACK1 = 2.1mm Barrel Jack with Terminal Block

nets:
  GND: Part3.GND, NEOPIXEL1.GND, IC1.IN, JACK1.NEG
  N1: Part3.D2, NEOPIXEL1.DI
  VIN: Part3.VIN, IC1.GND, JACK1.POS
  N2: NEOPIXEL1.+5V, IC1.OUT

custom parts:
  Arduino Nano 33 IoT: The Arduino Nano 33 IoT is a small, complete, and breadboard-friendly board based on the Arm® Cortex®-M0 32-bit SAMD21. It has onboard WiFi and Bluetooth® connectivity through a u-blox NINA-W10 chipset. Secure communication is ensured through the Microchip® ECC608 crypto chip. It also has 6-axis LSM6DS3 IMU.
  Neopixel Strip -- White (60/m): Neopixel Strip, White, 60 pixels per meter.
