# Fritzing sketch LabDigitalInOut (saved by Fritzing 0.9.0b)
breadboards: 1

parts:
  Arduino1 = Arduino Uno (Rev3)
  S1 = Pushbutton [package="[THT]"]
  R1 = Resistor [tolerance=±5% resistance=10k package=THT]
  R2 = Resistor [tolerance=±5% resistance=220 package=THT]
  R3 = Resistor [tolerance=±5% resistance=220 package=THT]
  LED1 = LED - 5mm [color="Red (633nm)" package="5 mm [THT]"]
  LED2 = LED - 5mm [color="Yellow (592nm)" package="5 mm [THT]"]

nets:
  N1: Arduino1.D2, S1.Pin_3, S1.Pin_4, R1.Pin_1
  N2: Arduino1.D3_PWM, R2.Pin_0
  N3: Arduino1.D4, R3.Pin_0
  N4: Arduino1.5V, S1.Pin_1, S1.Pin_2
  GND: Arduino1.GND, R1.Pin_0, LED1.cathode, LED2.cathode
  N5: R2.Pin_1, LED1.anode
  N6: R3.Pin_1, LED2.anode
