# Fritzing sketch LabDigitalInOutNano (saved by Fritzing 1.0.3b)
breadboards: 1

parts:
  S1 = Pushbutton [package="[THT]"]
  R1 = Resistor [tolerance=±5% resistance=10k power=0.25W package=THT]
  R2 = Resistor [tolerance=±5% resistance=220 power=0.25W package=THT]
  R3 = Resistor [tolerance=±5% resistance=220 power=0.25W package=THT]
  LED1 = LED - 5mm [color="Red (633nm)" current=0.030A package="5 mm [THT]"]
  LED2 = LED - 5mm [color="Yellow (592nm)" current=0.030A package="5 mm [THT]"]
  Part1 = Arduino Nano (Rev3.0)

nets:
  N1: S1.Pin_1, S1.Pin_2, Part1.3V3
  N2: S1.Pin_3, S1.Pin_4, R1.Pin_1, Part1.D2
  GND: R1.Pin_0, LED1.cathode, LED2.cathode, Part1.GND
  N3: R2.Pin_0, Part1.D3
  N4: R2.Pin_1, LED1.anode
  N5: R3.Pin_0, Part1.D4
  N6: R3.Pin_1, LED2.anode
