# Fritzing sketch LabHighCurrentLoadVDivider (saved by Fritzing 0.9.0b)
breadboards: 1

parts:
  DC_Motor = DC Motor
  TIP_120_Transistor = npn-Powertransistor [package="TO220 [THT]"]
  Resistor = Resistor [tolerance=±5% resistance=1k package=THT]
  Diode = Rectifier Diode [part_number=1N4001 package="Melf DO-213 AB [SMD]"]
  Power_plug = Power plug
  Voltage_Reg = Voltage Regulator [package=78xxl]
  Photoresistor = Photocell (LDR) [package=THT]
  Resistor_2 = Resistor [tolerance=±5% resistance=10k package=THT]

nets:
  N1: DC_Motor.pin_1, TIP_120_Transistor.collector, Diode.cathode
  N2: DC_Motor.pin_2, Power_plug.VCC, Voltage_Reg.IN
  N3: TIP_120_Transistor.base, Resistor.Pin_0
  GND: TIP_120_Transistor.emitter, Diode.anode, Power_plug.GND, Voltage_Reg.GND, Resistor_2.Pin_0
  N4: Resistor.Pin_1, Photoresistor.pin_0, Resistor_2.Pin_1
  N5: Voltage_Reg.OUT, Photoresistor.pin_1
