# Fritzing sketch LabTemplateNoArduino (saved by Fritzing 0.9.0b)
breadboards: 1

parts:
  Power_plug1 = Power plug
  IC1 = Voltage Regulator [package=78xxl]

nets:
  N1: Power_plug1.VCC, IC1.IN
  GND: Power_plug1.GND, IC1.GND
