# Fritzing sketch HBridgeNanoSwitch (saved by Fritzing 0.9.3b)
breadboards: 1

parts:
  Part3 = Arduino Nano (Rev3.0)
  S2 = Toggle Switch [package=THT]
  R2 = Resistor [tolerance=±5% resistance=10k package=THT]

nets:
  N1: Part3.GND, R2.Pin_1
  N2: Part3.D2, S2.L2, R2.Pin_0
  N3: Part3.3V3, S2.COM
