# Fritzing sketch HBridgeUnoSwitch (saved by Fritzing 0.9.3b)
breadboards: 1

parts:
  Arduino = Arduino Uno (Rev3)
  R1 = Resistor [tolerance=±5% resistance=10k package=THT]
  S1 = Toggle Switch [package=THT]

nets:
  N1: Arduino.D2, R1.Pin_1, S1.L2
  N2: Arduino.5V, S1.COM
  GND: Arduino.GND, R1.Pin_0
