# Fritzing sketch L9110HBridgeNano (saved by Fritzing 0.9.9b)
breadboards: 1

parts:
  M1 = DC Motor  # not connected
  C2 = Electrolytic Capacitor [capacitance=100µF voltage=35V package="1010 [SMD, electrolytic]"]
  JACK2 = 2.1mm Barrel Jack with Terminal Block
  R2 = Resistor [tolerance=±5% resistance=10k power=0.25 package=THT]
  S2 = Pushbutton [package="[THT]"]
  Part2 = Arduino Nano 33 IoT
  U1 = 555 Timer [package="SO8 [SMD]"]  # not connected

nets:
  N1: C2.-, JACK2.NEG, Part2.3V3
  N2: C2.+, R2.Pin_1, Part2.GND
  N3: JACK2.POS, Part2.VIN
  N4: R2.Pin_0, S2.Pin_1, S2.Pin_2
  N5: S2.Pin_3, S2.Pin_4

custom parts:
  Arduino Nano 33 IoT: The Arduino Nano 33 IoT is a small, complete, and breadboard-friendly board based on the Arm® Cortex®-M0 32-bit SAMD21. It has onboard WiFi and Bluetooth® connectivity through a u-blox NINA-W10 chipset. Secure communication is ensured through the Microchip® ECC608 crypto chip. It also has 6-axis LSM6DS3 IMU.
