# Fritzing sketch LabDCMotorTB6612 (saved by Fritzing 0.9.3b)
breadboards: 1

parts:
  Arduino = Arduino Uno (Rev3)
  R1 = Resistor [tolerance=±5% resistance=10k package=THT]
  C1 = Electrolytic Capacitor [capacitance=100µF package="1010 [SMD, electrolytic]"]
  S1 = Toggle Switch [package=THT]
  Part1 = Motor Driver 1A Dual TB6612FNG
  M1 = DC Motor
  JACK1 = 2.1mm Barrel Jack with Terminal Block

nets:
  N1: Arduino.D2, Part1.AIN1
  N2: Arduino.D3_PWM, Part1.AIN2
  N3: Arduino.D5_PWM, Part1.PWMA
  N4: Arduino.D7, R1.Pin_1, S1.L1
  3V3: Arduino.3V3, C1.+, S1.COM, Part1.VCC, Part1.STBY
  GND: Arduino.GND, R1.Pin_0, C1.-, Part1.GND, JACK1.NEG
  N5: Part1.A02, M1.pin_2
  N6: Part1.A01, M1.pin_1
  N7: Part1.VM, JACK1.POS
