# Fritzing sketch TB6612HBridge (saved by Fritzing 0.9.3b)
breadboards: 1

parts:
  Part1 = Motor Driver 1A Dual TB6612FNG  # not connected
  Part2 = Arduino MKR1000
  M1 = DC Motor  # not connected
  VCC1 = Battery block 9V
  R1 = Resistor [tolerance=±5% resistance=10k package="1206 [SMD]"]

nets:
  N1: Part2.VCC, R1.Pin_1
  N2: Part2.GND, VCC1.-

custom parts:
  Arduino MKR1000: MKR1000 is a powerful board that combines the functionality of the Zero and the Wi-Fi Shield. It is the ideal solution for makers wanting to design IoT projects with minimal previous experience in networking
