# Fritzing sketch TB6612HBridgeNano (saved by Fritzing 0.9.9b)
breadboards: 1

parts:
  Part1 = Motor Driver 1A Dual TB6612FNG  # not connected
  M1 = DC Motor  # not connected
  R1 = Resistor [tolerance=±5% resistance=10k package="1206 [SMD]"]
  C2 = Electrolytic Capacitor [capacitance=100µF voltage=35V package="1010 [SMD, electrolytic]"]
  JACK2 = 2.1mm Barrel Jack with Terminal Block
  R2 = Resistor [tolerance=±5% resistance=10k power=0.25 package=THT]
  S2 = Pushbutton [package="[THT]"]
  Part2 = Arduino Nano 33 IoT

nets:
  N1: R1.Pin_1, C2.-, JACK2.NEG, S2.Pin_3, S2.Pin_4, Part2.3V3
  N2: C2.+, R2.Pin_1, Part2.GND
  N3: JACK2.POS, Part2.VIN
  N4: R2.Pin_0, S2.Pin_1, S2.Pin_2

custom parts:
  Arduino Nano 33 IoT: The Arduino Nano 33 IoT is a small, complete, and breadboard-friendly board based on the Arm® Cortex®-M0 32-bit SAMD21. It has onboard WiFi and Bluetooth® connectivity through a u-blox NINA-W10 chipset. Secure communication is ensured through the Microchip® ECC608 crypto chip. It also has 6-axis LSM6DS3 IMU.
