# Fritzing sketch TB6612HBridgeUno (saved by Fritzing 0.9.3b)
breadboards: 1

parts:
  Arduino = Arduino Uno (Rev3)
  R1 = Resistor [tolerance=±5% resistance=10k package=THT]
  M1 = DC Motor
  C1 = Electrolytic Capacitor [capacitance=100µF package="1010 [SMD, electrolytic]"]
  S1 = Toggle Switch [package=THT]
  Part1 = Motor Driver 1A Dual TB6612FNG
  R2 = Resistor [tolerance=±5% resistance=10k package="1206 [SMD]"]
  JACK1 = 2.1mm Barrel Jack with Terminal Block

nets:
  N1: Arduino.D9_PWM, Part1.PWMA
  N2: Arduino.D2, R1.Pin_1, S1.L2
  N3: Arduino.D3_PWM, Part1.AIN1
  N4: Arduino.D4, Part1.AIN2
  5V: Arduino.5V, C1.+, S1.COM, Part1.VCC
  GND: Arduino.GND, R1.Pin_0, C1.-, Part1.GND, R2.Pin_1, JACK1.NEG
  N5: M1.pin_1, Part1.A02
  N6: M1.pin_2, Part1.A01
  N7: Part1.VM, JACK1.POS
  N8: Part1.STBY, R2.Pin_0
