# Fritzing sketch LabHighCurrentArduinoMotor (saved by Fritzing 0.9.3b)
breadboards: 1

parts:
  Arduino1 = Arduino Uno (Rev3)
  Potentiometer = POT [package=alps_pot]
  TIP_120_Transistor = npn-Powertransistor [package="TO220 [THT]"]
  Motor = DC Motor
  Diode = Rectifier Diode [part_number=1N4001 package="Melf DO-213 AB [SMD]"]
  JACK1 = 2.1mm Barrel Jack with Terminal Block
  R1 = Resistor [tolerance=±5% resistance=1k package=THT]

nets:
  N1: Arduino1.A0, Potentiometer.S
  N2: Arduino1.D9_PWM, R1.Pin_1
  N3: Arduino1.5V, Potentiometer.E
  GND: Arduino1.GND, Potentiometer.A, TIP_120_Transistor.emitter, Diode.anode, JACK1.NEG
  N4: TIP_120_Transistor.base, R1.Pin_0
  N5: TIP_120_Transistor.collector, Motor.pin_2, Diode.cathode
  N6: Motor.pin_1, JACK1.POS
