# Fritzing sketch LabHighCurrentNanoMotor (saved by Fritzing 0.9.3b)
breadboards: 1

parts:
  Potentiometer = POT [package=alps_pot]
  TIP_120_Transistor = npn-Powertransistor [package="TO220 [THT]"]
  Motor = DC Motor
  Diode = Rectifier Diode [part_number=1N4001 package="Melf DO-213 AB [SMD]"]
  JACK1 = 2.1mm Barrel Jack with Terminal Block
  R1 = Resistor [tolerance=±5% resistance=1k package=THT]

nets:
  GND: Potentiometer.A, TIP_120_Transistor.emitter, Diode.anode, JACK1.NEG
  N1: TIP_120_Transistor.base, R1.Pin_0
  N2: TIP_120_Transistor.collector, Motor.pin_2, Diode.cathode
  N3: Motor.pin_1, JACK1.POS
