# Fritzing sketch I2S_amp_circuit_MAX98357_nano_simple (saved by Fritzing 0.9.8b)
breadboards: 1

parts:
  SparkFun_I2S_Audio_Breakout2 = SparkFun_I2S_Audio_Breakout
  Part3 = Arduino Nano (Rev3.0)
  TRS1 = Audio Jack (TRS) 3.5mm [package="4Ucon 08780 [THT]"]
  microSD_Transflash1 = SparkFun - microSD Transflash
  Breakout_Board2 = Level Shifting uSD Breakout [package="DIP (Dual Inline) [THT]"]  # not connected
  Part4 = Adafruit MicroSD card breakout board [part_number="Adafruit #254"]  # not connected

nets:
  N1: SparkFun_I2S_Audio_Breakout2.OUT+, TRS1.Ring, TRS1.Tip
  N2: SparkFun_I2S_Audio_Breakout2.OUT-, TRS1.Sleeve
  GND: Part3.GND, microSD_Transflash1.GND
  N3: Part3.D10, microSD_Transflash1.CS
  N4: Part3.D11/MOSI, microSD_Transflash1.DI
  N5: Part3.D12/MISO, microSD_Transflash1.DO
  3V3: Part3.3V3, microSD_Transflash1.VCC
  N6: Part3.D13/SCK, microSD_Transflash1.SCK

custom parts:
  SparkFun_I2S_Audio_Breakout: The SparkFun I2S Audio Breakout board uses the MAX98357A digital to analog converter (DAC), which converts I2S (not be confused with I2C) audio to an analog signal to drive speakers. The I2S Audio Breakout converts the digital audio signals using the I2S standard to an analog signal and amplifies the signal using a class D amplifier which can deliver up to 3.2W of power into a 4Ω load. The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
  Level Shifting uSD Breakout: Breakout board for the TI TXB0104 bi-directional level shifter IC. VccA should be lower than VccB. VccA can range from 1.2V to 3.6V, and VCCB can range from 1.65V to 5.5V.
  Adafruit MicroSD card breakout board: Not just a simple breakout board, this microSD adapter goes the extra mile - designed for ease of use. Onboard 5v->3v regulator provides 150mA for power-hungry cards 3v level shifting means you can use this with ease on either 3v or 5v systems Uses a proper level shifting chip, not resistors: less problems, and faster read/write access Use 3 or 4 digital pins to read and write 2Gb+ of storage!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
