# Fritzing sketch NanoLIS3DH (saved by Fritzing 0.9.3b)
breadboards: 1

parts:
  Accelerometer1 = SparkFun_LIS3DH-Breakout [part_number=SEN-13963]
  Part1 = Arduino Nano (Rev3.0) (ICSP)

nets:
  N1: Accelerometer1.GND, Accelerometer1.SA0
  N2: Part1.A6, Part1.A5

custom parts:
  SparkFun_LIS3DH-Breakout: The LIS3DH Breakout is a smart, low-power, three-axis, capacitive micro-machined accelerometer with 12 bits of resolution that you can use to add translation detection to your project. It would be classified as a 3DoF, or 3 Degrees of Freedom. Inertial Measurement Units (or IMUs) can provide additional space location data, such as gyroscopic or magnetometric. The LIS3DH provided on this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
