# Fritzing sketch UnoLIS3DH (saved by Fritzing 0.9.3b)
breadboards: 1

parts:
  Arduino1 = Arduino Uno (Rev3)
  Accelerometer1 = SparkFun_LIS3DH-Breakout [part_number=SEN-13963]

nets:
  N1: Arduino1.A4/SDA, Accelerometer1.SDA
  N2: Arduino1.A5/SCL, Accelerometer1.SCL
  GND: Arduino1.GND, Accelerometer1.GND, Accelerometer1.SA0
  3V3: Arduino1.3V3, Accelerometer1.VCC

custom parts:
  SparkFun_LIS3DH-Breakout: The LIS3DH Breakout is a smart, low-power, three-axis, capacitive micro-machined accelerometer with 12 bits of resolution that you can use to add translation detection to your project. It would be classified as a 3DoF, or 3 Degrees of Freedom. Inertial Measurement Units (or IMUs) can provide additional space location data, such as gyroscopic or magnetometric. The LIS3DH provided on this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
