# Fritzing sketch LabInterval (saved by Fritzing 0.9.3b)
breadboards: 1

parts:
  Part1 = Arduino Uno (Rev3) - ICSP
  S1 = Pushbutton [package="[THT]"]
  S2 = Pushbutton [package="[THT]"]
  S3 = Pushbutton [package="[THT]"]
  LED1 = smd LED [color="Red (633nm)" package="0805 [SMD]"]
  R1 = Resistor [tolerance=±5% resistance=220 package="0402 [SMD]"]
  R2 = Resistor [tolerance=±5% resistance=220 package="0402 [SMD]"]
  R3 = Resistor [tolerance=±5% resistance=220 package="0402 [SMD]"]
  LED2 = smd LED [color="Blue (430nm)" package="0805 [SMD]"]
  LED3 = smd LED [color="Green (565nm)" package="0805 [SMD]"]
  R4 = Resistor [tolerance=±5% resistance=10k package="0402 [SMD]"]
  R5 = Resistor [tolerance=±5% resistance=10k package="0402 [SMD]"]
  R6 = Resistor [tolerance=±5% resistance=10k package="0402 [SMD]"]

nets:
  N1: Part1.5V, S1.Pin_3, S1.Pin_4, S2.Pin_1, S2.Pin_2, S3.Pin_1, S3.Pin_2
  N2: Part1.D9_PWM, R1.Pin_0
  N3: Part1.D10_PWM/SS, R2.Pin_0
  N4: Part1.D11_PWM/MOSI, R3.Pin_0
  GND: Part1.GND, LED1.cathode, LED2.cathode, LED3.cathode, R4.Pin_1, R5.Pin_1, R6.Pin_1
  N5: Part1.D2, S1.Pin_1, S1.Pin_2, R6.Pin_0
  N6: Part1.D3_PWM, S2.Pin_3, S2.Pin_4, R4.Pin_0
  N7: Part1.D4, S3.Pin_3, S3.Pin_4, R5.Pin_0
  N8: LED1.anode, R1.Pin_1
  N9: R2.Pin_1, LED3.anode
  N10: R3.Pin_1, LED2.anode
