# Fritzing sketch Nano_SSD1306_OLED (saved by Fritzing 0.9.8b)
breadboards: 1

parts:
  Part2 = Arduino Nano 33 IoT
  U1 = POT [package=alps_pot]
  o1 = Module display OLED I2C 128x64 SSD1306 [package=THT]

nets:
  GND: Part2.GND, U1.A, o1.GND
  N1: Part2.A5/SCL, o1.SCL
  N2: Part2.A4/SDA, o1.SDA
  N3: Part2.A0, U1.S
  3V3: Part2.3V3, U1.E, o1.VCC

custom parts:
  Arduino Nano 33 IoT: The Arduino Nano 33 IoT is a small, complete, and breadboard-friendly board based on the Arm® Cortex®-M0 32-bit SAMD21. It has onboard WiFi and Bluetooth® connectivity through a u-blox NINA-W10 chipset. Secure communication is ensured through the Microchip® ECC608 crypto chip. It also has 6-axis LSM6DS3 IMU.
  Module display OLED I2C 128x64 SSD1306: Ecran OLED I2C SSD163 de 128x64 avec connexion I2C
