# Fritzing sketch EncoderPushbuttonNano (saved by Fritzing 0.9.4)
breadboards: 1

parts:
  Part1 = Arduino Nano 33 IoT
  RE1 = Rotary Encoder [package=THT]

nets:
  N1: Part1.GND, RE1.EncoderPinC
  N2: Part1.D2, RE1.EncoderPinB
  N3: Part1.D3, RE1.EncoderPinA

custom parts:
  Arduino Nano 33 IoT: The Arduino Nano 33 IoT is a small, complete, and breadboard-friendly board based on the Arm® Cortex®-M0 32-bit SAMD21. It has onboard WiFi and Bluetooth® connectivity through a u-blox NINA-W10 chipset. Secure communication is ensured through the Microchip® ECC608 crypto chip. It also has 6-axis LSM6DS3 IMU.
