# Fritzing sketch EncoderPushbuttonUno (saved by Fritzing 0.9.4)
breadboards: 1

parts:
  Arduino1 = Arduino Uno (Rev3)
  RE2 = Rotary Encoder [package=THT]

nets:
  N1: Arduino1.D2, RE2.EncoderPinA
  N2: Arduino1.D3_PWM, RE2.EncoderPinB
  GND: Arduino1.GND, RE2.EncoderPinC
