# Fritzing sketch nano_sd_card_DHT11 (saved by Fritzing 0.9.4)
breadboards: 1

parts:
  Part3 = Arduino Nano (Rev3.0)
  Breakout_Board1 = Level Shifting uSD Breakout [package="DIP (Dual Inline) [THT]"]  # not connected
  DHT1 = DHT11 Humitidy and Temperature Sensor
  R1 = Resistor [tolerance=±5% resistance=10k package="1206 [SMD]"]

nets:
  GND: Part3.GND, DHT1.GND
  N1: Part3.A0, DHT1.DATA, R1.Pin_1
  3V3: Part3.3V3, DHT1.VDD, R1.Pin_0

custom parts:
  Level Shifting uSD Breakout: Breakout board for the TI TXB0104 bi-directional level shifter IC. VccA should be lower than VccB. VccA can range from 1.2V to 3.6V, and VCCB can range from 1.65V to 5.5V.
  DHT11 Humitidy and Temperature Sensor: DHT11 Humidity and Temperature Sensor
