# Fritzing sketch nano_sd_card_apds9960 (saved by Fritzing 0.9.4)
breadboards: 1

parts:
  Part3 = Arduino Nano (Rev3.0)
  Breakout_Board1 = Level Shifting uSD Breakout [package="DIP (Dual Inline) [THT]"]  # not connected
  Part4 = Adafruit APDS-9960 [part_number="Adafruit #3595"]

nets:
  GND: Part3.GND, Part4.GND
  N1: Part3.A5, Part4.SCL
  N2: Part3.A4, Part4.SDA
  3V3: Part3.3V3, Part4.VIN

custom parts:
  Level Shifting uSD Breakout: Breakout board for the TI TXB0104 bi-directional level shifter IC. VccA should be lower than VccB. VccA can range from 1.2V to 3.6V, and VCCB can range from 1.65V to 5.5V.
  Adafruit APDS-9960: The APDS9960 from Avago Technologies has an integrated IR LED and driver, along with four directional photodiodes that sense reflected IR energy from the LED. It's proximity detection feature allows it to measure the distance an object is from the front of the sensor (up to a few centimeters) with 8 bit resolution. Since there are four IR sensors, you can measure the changes in light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
