# Fritzing sketch nano_sd_card_tmp36 (saved by Fritzing 0.9.4)
breadboards: 1

parts:
  Part3 = Arduino Nano (Rev3.0)
  Breakout_Board1 = Level Shifting uSD Breakout [package="DIP (Dual Inline) [THT]"]  # not connected
  T1 = TMP36 Temperature Sensor [package="TO92 [THT]"]

nets:
  GND: Part3.GND, T1.GND
  N1: Part3.A0, T1.Vout
  N2: Part3.3V3, T1.+Vs

custom parts:
  Level Shifting uSD Breakout: Breakout board for the TI TXB0104 bi-directional level shifter IC. VccA should be lower than VccB. VccA can range from 1.2V to 3.6V, and VCCB can range from 1.65V to 5.5V.
