# Fritzing sketch LabSTSPIN220StepperNanoExtSupply (saved by Fritzing 0.9.9b)
breadboards: 1

parts:
  Part3 = Arduino Nano 33 IoT
  Pololu_A1 = Pololu A4988 [package=SO16]
  MOTOR1 = Adafruit Gear-Reduced Stepper Motor (small)
  C14 = Capacitor Polarized [package=cpol-radial-100uf-25v]
  JACK1 = 2.1mm Barrel Jack with Terminal Block
  R2 = Resistor [tolerance=±5% power=0.25 resistance=10k package=THT]

nets:
  GND: Part3.GND, Pololu_A1.ENABLE, Pololu_A1.MS1, Pololu_A1.MS2, Pololu_A1.GND, C14.-, JACK1.NEG
  N1: Part3.D2, Pololu_A1.STEP
  N2: Part3.D3, Pololu_A1.DIR
  N3: Part3.VIN, Pololu_A1.VMOT, JACK1.POS
  3V3: Part3.3V3, Pololu_A1.VDD, C14.+, R2.Pin_0
  N4: Pololu_A1.SLEEP, R2.Pin_1
  N5: Pololu_A1.1B, MOTOR1.BLUE
  N6: Pololu_A1.1A, MOTOR1.YELLOW
  N7: Pololu_A1.2A, MOTOR1.PINK
  N8: Pololu_A1.2B, MOTOR1.ORANGE

custom parts:
  Arduino Nano 33 IoT: The Arduino Nano 33 IoT is a small, complete, and breadboard-friendly board based on the Arm® Cortex®-M0 32-bit SAMD21. It has onboard WiFi and Bluetooth® connectivity through a u-blox NINA-W10 chipset. Secure communication is ensured through the Microchip® ECC608 crypto chip. It also has 6-axis LSM6DS3 IMU.
  Adafruit Gear-Reduced Stepper Motor (small): Adafruit gear-reduction stepper motor (small)
