# Fritzing sketch LabSTSPIN220StepperUno (saved by Fritzing 0.9.9b)
breadboards: 1

parts:
  Arduino1 = Arduino Uno (Rev3)
  Pololu_A2 = Pololu A4988 [package=SO16]
  MOTOR2 = Adafruit Gear-Reduced Stepper Motor (small)
  C15 = Capacitor Polarized [package=cpol-radial-100uf-25v]
  R1 = Resistor [tolerance=±5% power=0.25 resistance=10k package=THT]

nets:
  N1: Arduino1.D2, Pololu_A2.STEP
  N2: Arduino1.D3_PWM, Pololu_A2.DIR
  5V: Arduino1.5V, Pololu_A2.VDD, Pololu_A2.VMOT, C15.+, R1.Pin_0
  GND: Arduino1.GND, Pololu_A2.ENABLE, Pololu_A2.MS1, Pololu_A2.MS2, Pololu_A2.GND, C15.-
  N3: Pololu_A2.SLEEP, R1.Pin_1
  N4: Pololu_A2.1B, MOTOR2.BLUE
  N5: Pololu_A2.1A, MOTOR2.YELLOW
  N6: Pololu_A2.2A, MOTOR2.PINK
  N7: Pololu_A2.2B, MOTOR2.ORANGE

custom parts:
  Adafruit Gear-Reduced Stepper Motor (small): Adafruit gear-reduction stepper motor (small)
