# Fritzing sketch TB6612HBridgeStepperNano_ext_power_2 (saved by Fritzing 0.9.9b)
breadboards: 1

parts:
  Part1 = Motor Driver 1A Dual TB6612FNG  # not connected
  MOTOR1 = Adafruit Gear-Reduced Stepper Motor (small)  # not connected
  Part2 = Arduino Nano 33 IoT
  C1 = Capacitor Polarized [package=cpol-radial-10uf-25v]
  R1 = Resistor [tolerance=±5% resistance=10k package="2010 [SMD]"]
  U1 = Voltage Regulator - 5V [package="DPak [SMD]"]  # not connected

nets:
  N1: Part2.GND, C1.-
  N2: Part2.3V3, C1.+, R1.Pin_1

notes:
  Flip motor vertically after exporting to SVG

custom parts:
  Adafruit Gear-Reduced Stepper Motor (small): Adafruit gear-reduction stepper motor (small)
  Arduino Nano 33 IoT: The Arduino Nano 33 IoT is a small, complete, and breadboard-friendly board based on the Arm® Cortex®-M0 32-bit SAMD21. It has onboard WiFi and Bluetooth® connectivity through a u-blox NINA-W10 chipset. Secure communication is ensured through the Microchip® ECC608 crypto chip. It also has 6-axis LSM6DS3 IMU.
