# Fritzing sketch TB6612HBridgeStepperUno (saved by Fritzing 0.9.9b)
breadboards: 1

parts:
  Arduino1 = Arduino Uno (Rev3)
  MOTOR2 = Adafruit Gear-Reduced Stepper Motor (small)
  C1 = Capacitor Polarized [package=cpol-radial-10uf-25v]
  Part3 = Motor Driver 1A Dual TB6612FNG

nets:
  N1: Arduino1.D8, Part3.BIN2
  N2: Arduino1.D9_PWM, Part3.BIN1
  N3: Arduino1.D10_PWM/SS, Part3.AIN2
  N4: Arduino1.D11_PWM/MOSI, Part3.AIN1
  GND: Arduino1.GND, C1.-, Part3.GND
  5V: Arduino1.5V, C1.+, Part3.VCC
  N5: Arduino1.VIN, Part3.VM
  N6: MOTOR2.RED, MOTOR2.ORANGE

custom parts:
  Adafruit Gear-Reduced Stepper Motor (small): Adafruit gear-reduction stepper motor (small)
