# Fritzing sketch LabSPI (saved by Fritzing 0.9.0b)
breadboards: 1

parts:
  Arduino1 = Arduino Uno (Rev3)
  R1 = Resistor [tolerance=±20% resistance=100 package=THT]
  SP1 = SPEAKER [package=pcb_mount_speaker]
  U1 = AD5206 Digital Potentiometer [maximum_resistance=10kΩ package="DIP28 [THT]"]

nets:
  N1: Arduino1.D9_PWM, SP1.-
  N2: Arduino1.D10_PWM/SS, U1.CS
  N3: Arduino1.D11_PWM/MOSI, U1.SDI
  N4: Arduino1.D13/SCK, U1.CLK
  5V: Arduino1.5V, U1.Vdd
  GND: Arduino1.GND, U1.Gnd, U1.Vss, U1.A5
  N5: R1.Pin_0, SP1.+
  N6: R1.Pin_1, U1.W5
