# Fritzing sketch Vl53L0X-Nano (saved by Fritzing 0.9.4)
breadboards: 1

parts:
  Part1 = Arduino Nano 33 IoT
  Part2 = Adafruit VL53L0X Time of Flight Distance Sensor [part_number="Adafruit #3317"]

nets:
  GND: Part1.GND, Part2.GND
  N1: Part1.A5/SCL, Part2.SCL
  N2: Part1.A4/SDA, Part2.SDA
  3V3: Part1.3V3, Part2.VIN

custom parts:
  Arduino Nano 33 IoT: The Arduino Nano 33 IoT is a small, complete, and breadboard-friendly board based on the Arm® Cortex®-M0 32-bit SAMD21. It has onboard WiFi and Bluetooth® connectivity through a u-blox NINA-W10 chipset. Secure communication is ensured through the Microchip® ECC608 crypto chip. It also has 6-axis LSM6DS3 IMU.
  Adafruit VL53L0X Time of Flight Distance Sensor: The VL53L0X is a Time of Flight distance sensor like no other you've used! The sensor contains a very tiny invisible laser source, and a matching sensor. The VL53L0X can detect the "time of flight", or how long the light has taken to bounce back to the sensor. Since it uses a very narrow light source, it is good for determining distance of only the surface directly in front of it. Unlike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
