# Fritzing sketch APDS-9960-Nano (saved by Fritzing 0.9.4)
breadboards: 1

parts:
  Part1 = Arduino Nano 33 IoT
  PART1 = APDS-9960 RGB and Gesture Sensor [part_number=SEN-12787]

nets:
  GND: Part1.GND, PART1.GND
  N1: Part1.A5/SCL, PART1.SCL
  N2: Part1.A4/SDA, PART1.SDA
  N3: Part1.3V3, PART1.VL

custom parts:
  Arduino Nano 33 IoT: The Arduino Nano 33 IoT is a small, complete, and breadboard-friendly board based on the Arm® Cortex®-M0 32-bit SAMD21. It has onboard WiFi and Bluetooth® connectivity through a u-blox NINA-W10 chipset. Secure communication is ensured through the Microchip® ECC608 crypto chip. It also has 6-axis LSM6DS3 IMU.
  APDS-9960 RGB and Gesture Sensor: Breakout board for the Avago APDS-9960 proximity, light, RGB, and gesture sensors. Please visit www.sparkfun.com to learn more.
