# Fritzing sketch NanoExternalPower (saved by Fritzing 0.9.4)
breadboards: 1

parts:
  Part3 = Arduino Nano 33 IoT
  JACK1 = 2.1mm Barrel Jack with Terminal Block
  IC1 = Voltage Regulator [package=to220-igo]

nets:
  N1: Part3.GND, JACK1.NEG, IC1.IN
  VIN: Part3.VIN, JACK1.POS, IC1.GND

custom parts:
  Arduino Nano 33 IoT: The Arduino Nano 33 IoT is a small, complete, and breadboard-friendly board based on the Arm® Cortex®-M0 32-bit SAMD21. It has onboard WiFi and Bluetooth® connectivity through a u-blox NINA-W10 chipset. Secure communication is ensured through the Microchip® ECC608 crypto chip. It also has 6-axis LSM6DS3 IMU.
