# Fritzing sketch HC-SR04Ultrasonic_Nano (saved by Fritzing 0.9.4)
breadboards: 1

parts:
  HC-SR04_Sensor_1 = HC-SR04 Ultrasonic Distance Sensor
  Part1 = Arduino Nano 33 IOT

nets:
  VCC: HC-SR04_Sensor_1.VCC, Part1.VIN
  N1: HC-SR04_Sensor_1.TRIG, Part1.D9~
  N2: HC-SR04_Sensor_1.ECHO, Part1.D10~
  GND: HC-SR04_Sensor_1.GND, Part1.GND, Part1.D13~
  N3: Part1.RESET, Part1.A7
  N4: Part1.D11/MOSI, Part1.+5V

custom parts:
  Arduino Nano 33 IOT: The Arduino Nano 33 IoT is the easiest and cheapest point of entry to enhance existing devices (and creating new ones) to be part of the IoT and designing pico-network applications. Whether you are looking at building a sensor network connected to your office or home router, or if you want to create a BLE device sending data to a cellphone, the Nano 33 IoT is your one-stop-solution for many of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
