# Fritzing sketch HC-SR04Ultrasonic_Uno (saved by Fritzing 0.9.4)
breadboards: 1

parts:
  Arduino1 = Arduino Uno (Rev3)
  HC-SR04_Sensor_1 = HC-SR04 Ultrasonic Distance Sensor

nets:
  N1: Arduino1.D9_PWM, HC-SR04_Sensor_1.TRIG
  N2: Arduino1.D10_PWM/SS, HC-SR04_Sensor_1.ECHO
  5V: Arduino1.5V, HC-SR04_Sensor_1.VCC
  GND: Arduino1.GND, HC-SR04_Sensor_1.GND
