# Fritzing sketch LabSerialDuplex (saved by Fritzing 0.9.0b)
breadboards: 1

parts:
  Arduino1 = Arduino Uno (Rev3)
  S1 = Round Pushbutton
  Part1 = Triple Axis Accelerometer Breakout - ADXL335
  R1 = Resistor [tolerance=±5% resistance=10k package=THT]

nets:
  N1: Arduino1.A0, Part1.YOUT
  N2: Arduino1.A1, Part1.XOUT
  GND: Arduino1.GND, Part1.GND, R1.Pin_0
  N3: Arduino1.D2, S1.leg1, R1.Pin_1
  5V: Arduino1.5V, S1.leg0, Part1.VCC
