# Fritzing sketch LabSerialDuplexNano (saved by Fritzing 0.9.3b)
breadboards: 1

parts:
  Part1 = Triple Axis Accelerometer Breakout - ADXL335
  R1 = Resistor [tolerance=±5% resistance=10k package=THT]
  S2 = Pushbutton [package="[THT]"]
  Part2 = Arduino Nano (Rev3.0) (ICSP)

nets:
  N1: Part1.YOUT, Part2.A1
  N2: Part1.XOUT, Part2.A0
  GND: Part1.GND, R1.Pin_1, Part2.GND
  VCC: Part1.VCC, S2.Pin_1, S2.Pin_2, Part2.D2, Part2.3V3
  N3: R1.Pin_0, S2.Pin_3, S2.Pin_4
