# Fritzing sketch LabSerial (saved by Fritzing 0.9.0b)
breadboards: 1

parts:
  Arduino1 = Arduino Uno (Rev3)
  U1 = POT [package=alps_pot]

nets:
  N1: Arduino1.A0, U1.S
  GND: Arduino1.GND, U1.A
  N2: Arduino1.5V, U1.E
