# Fritzing sketch Nano_2_pots_button (saved by Fritzing 0.9.4)
breadboards: 1

parts:
  Part3 = Arduino Nano 33 IoT
  U1 = POT [package=alps_pot]
  U2 = POT [package=alps_pot]
  S1 = Pushbutton [package="[THT]"]
  R1 = Resistor [tolerance=±5% resistance=10k package="2512 [SMD]"]

nets:
  GND: Part3.GND, U1.A, U2.A, R1.Pin_1
  N1: Part3.D2, S1.Pin_1, S1.Pin_2
  N2: Part3.A1, U2.S
  N3: Part3.A0, U1.S
  N4: Part3.3V3, U1.E, U2.E
  N5: S1.Pin_3, S1.Pin_4, R1.Pin_0

custom parts:
  Arduino Nano 33 IoT: The Arduino Nano 33 IoT is a small, complete, and breadboard-friendly board based on the Arm® Cortex®-M0 32-bit SAMD21. It has onboard WiFi and Bluetooth® connectivity through a u-blox NINA-W10 chipset. Secure communication is ensured through the Microchip® ECC608 crypto chip. It also has 6-axis LSM6DS3 IMU.
