# Fritzing sketch Uno_2_pots_button (saved by Fritzing 0.9.8b)
breadboards: 1

parts:
  Arduino1 = Arduino Uno (Rev3)
  S1 = Pushbutton [package="[THT]"]
  RE1 = Rotary Encoder [package=THT]
  RE2 = Rotary Encoder [package=THT]
  R1 = Resistor [tolerance=±5% resistance=10k power=0.25 package=THT]

nets:
  N1: Arduino1.A0, RE2.EncoderPinC
  N2: Arduino1.A1, RE1.EncoderPinC
  N3: Arduino1.D2, S1.Pin_3, S1.Pin_4, R1.Pin_0
  5V: Arduino1.5V, S1.Pin_1, S1.Pin_2, RE1.EncoderPinA, RE2.EncoderPinA
  GND: Arduino1.GND, RE1.EncoderPinB, RE2.EncoderPinB, R1.Pin_1
