# Fritzing sketch LabServoNano (saved by Fritzing 0.9.9b)
breadboards: 1

parts:
  R2 = Basic Force Sensing Resistor (FSR) [package=THT]
  R1 = Resistor [tolerance=±5% resistance=10k power=0.25 package=THT]
  Part1 = Arduino Nano (Rev3.0) (ICSP)
  J2 = Basic Servo
  C3 = Electrolytic Capacitor [capacitance=10μF voltage=35V package="0605 [SMD, electrolytic]"]

nets:
  N1: R2.pin_0, Part1.3V3, C3.+
  N2: R2.pin_1, R1.Pin_1, Part1.AREF
  GND: R1.Pin_0, Part1.GND, J2.gnd, C3.-
  N3: Part1.D9, J2.pulse
  VIN: Part1.VIN, J2.vcc
