# Fritzing sketch BipolarStepperLab (saved by Fritzing 0.9.0b)
breadboards: 1

parts:
  H-Bridge = L293D [package=THT]
  12V_Power_supply = 2.1mm Barrel Jack with Terminal Block
  Arduino = Arduino Uno (Rev3)
  M1 = Stepper Motor - Bipolar

nets:
  5V: H-Bridge.Enable_1, H-Bridge.Enable_2, H-Bridge.+V, Arduino.5V
  N1: H-Bridge.In_1, Arduino.D8
  Motor wire B: H-Bridge.Out_1_(_Controlled_by_Enable_1_), M1.B
  GND: H-Bridge.0V, 12V_Power_supply.NEG, Arduino.GND
  Motor wire D: H-Bridge.Out_2_(_Controlled_by_Enable_1_), M1.D
  N2: H-Bridge.In_2, Arduino.D9_PWM
  12V: H-Bridge.+Vmotor, 12V_Power_supply.POS
  N3: H-Bridge.In_3, Arduino.D10_PWM/SS
  N4: H-Bridge.Out_3_(_Controlled_by_Enable_2_), M1.C
  N5: H-Bridge.Out_4_(_Controlled_by_Enable_2_), M1.A
  N6: H-Bridge.In_4, Arduino.D11_PWM/MOSI
