# Fritzing sketch UnipolarStepperLab2 (saved by Fritzing 0.8.0b)
breadboards: 1

parts:
  Arduino = Arduino Uno (Rev3)
  Unipolar_Stepper = Adafruit Gear-Reduced Stepper Motor (small)
  12V_Power_supply = 2.1mm Barrel Jack with Terminal Block
  IC1 = ULN2003A [package="DIP16 [THT]"]
  D1 = Rectifier Diode [part_number=1N4001 package="300 mil [THT]"]

nets:
  N1: Arduino.GND, 12V_Power_supply.NEG, IC1.0V
  N2: Arduino.D8, IC1.In_4
  N3: Arduino.D9_PWM, IC1.In_3
  N4: Arduino.D10_PWM/SS, IC1.In_2
  N5: Arduino.D11_PWM/MOSI, IC1.In_1
  N6: Unipolar_Stepper.RED, IC1.COM_-_Common, D1.cathode
  N7: Unipolar_Stepper.ORANGE, IC1.Out_1
  N8: Unipolar_Stepper.YELLOW, IC1.Out_2
  N9: Unipolar_Stepper.PINK, IC1.Out_3
  N10: Unipolar_Stepper.BLUE, IC1.Out_4
  N11: 12V_Power_supply.POS, D1.anode

custom parts:
  Adafruit Gear-Reduced Stepper Motor (small): Adafruit gear-reduction stepper motor (small)
