# Fritzing sketch LabSwitchesSerial (saved by Fritzing 0.9.0b)
breadboards: 1

parts:
  Power_plug1 = Power plug
  IC1 = Voltage Regulator [package=78xxl]
  S1 = Pushbutton [package="[THT]"]
  S2 = Pushbutton [package="[THT]"]
  S3 = Pushbutton [package="[THT]"]
  LED1 = LED - 5mm [color="Red (633nm)" package="5 mm [THT]"]
  R1 = Resistor [tolerance=±5% resistance=220 package=THT]

nets:
  N1: Power_plug1.VCC, IC1.IN
  GND: Power_plug1.GND, IC1.GND, LED1.cathode
  N2: IC1.OUT, R1.Pin_0
  N3: S1.Pin_1, S1.Pin_2, R1.Pin_1
  N4: S1.Pin_3, S1.Pin_4, S2.Pin_1, S2.Pin_2
  N5: S2.Pin_3, S2.Pin_4, S3.Pin_1, S3.Pin_2
  N6: S3.Pin_3, S3.Pin_4, LED1.anode
