# Fritzing sketch LabSwitchesMotor (saved by Fritzing 0.9.0b)
breadboards: 1

parts:
  Power_plug1 = Power plug
  IC1 = Voltage Regulator [package=78xxl]
  S2 = Pushbutton [package="[THT]"]
  LED1 = LED - 5mm [color="Red (633nm)" package="5 mm [THT]"]
  M1 = DC Motor
  R1 = Resistor [tolerance=±5% resistance=220 package=THT]

nets:
  N1: Power_plug1.VCC, IC1.IN
  GND: Power_plug1.GND, IC1.GND, LED1.cathode, M1.pin_1
  N2: IC1.OUT, S2.Pin_1, S2.Pin_2
  N3: S2.Pin_3, S2.Pin_4, M1.pin_2, R1.Pin_1
  N4: LED1.anode, R1.Pin_0
