# Fritzing sketch LabToneAudioJackNano (saved by Fritzing 0.9.4)
breadboards: 1

parts:
  Part1 = Arduino Nano (Rev3.0)
  R4 = Resistor [tolerance=±5% resistance=10k package=THT]
  TRS1 = Audio Jack (TRS) 3.5mm [package="4Ucon 08780 [THT]"]

nets:
  N1: Part1.D8, TRS1.Tip
  N2: R4.Pin_1, TRS1.Sleeve
