# Fritzing sketch LabToneSimple (saved by Fritzing 0.9.4)
breadboards: 1

parts:
  Arduino1 = Arduino Uno (Rev3)
  R3 = Resistor [tolerance=±5% resistance=100 package=THT]
  SPKR1 = Loudspeaker
  Variable_Resistor = Basic Force Sensing Resistor (FSR) [package=THT]
  part = Resistor [tolerance=±5% resistance=10k package=THT]

nets:
  N1: Arduino1.A0, Variable_Resistor.pin_1, part.Pin_1
  N2: Arduino1.D8, SPKR1.pin2
  N3: Arduino1.5V, Variable_Resistor.pin_0
  GND: Arduino1.GND, R3.Pin_0, part.Pin_0
  N4: R3.Pin_1, SPKR1.pin1
