# Fritzing sketch LabToneSimpleNano (saved by Fritzing 0.9.3b)
breadboards: 1

parts:
  R3 = Resistor [tolerance=±5% resistance=100 package=THT]
  SPKR1 = Loudspeaker
  J1 = Basic Force Sensing Resistor (FSR) [package=THT]
  J2 = Basic Force Sensing Resistor (FSR) [package=THT]
  Part1 = Arduino Nano (Rev3.0)

nets:
  GND: R3.Pin_0, J2.pin_1
  N1: R3.Pin_1, SPKR1.pin1
  N2: SPKR1.pin2, Part1.D8
  N3: J1.pin_1, J2.pin_0, Part1.A0
