# Fritzing sketch LabToneAudioJack (saved by Fritzing 0.9.4)
breadboards: 1

parts:
  R3 = Resistor [tolerance=±5% resistance=100 package=THT]
  SPKR1 = Loudspeaker
  Q2 = npn-Powertransistor [package="TO220 [THT]"]

nets:
  GND: R3.Pin_0, Q2.collector
  N1: R3.Pin_1, SPKR1.pin1
