# Fritzing sketch LabToneInstrument (saved by Fritzing 0.9.0b)
breadboards: 1

parts:
  Arduino1 = Arduino Uno (Rev3)
  R7 = Resistor [tolerance=±5% resistance=100 package=THT]
  SPKR1 = Loudspeaker
  R1 = Basic Force Sensing Resistor (FSR) [package=THT]
  R2 = Basic Force Sensing Resistor (FSR) [package=THT]
  R3 = Basic Force Sensing Resistor (FSR) [package=THT]
  R4 = Resistor [tolerance=±5% resistance=10k package=THT]
  R5 = Resistor [tolerance=±5% resistance=10k package=THT]
  R6 = Resistor [tolerance=±5% resistance=10k package=THT]

nets:
  N1: Arduino1.A0, R2.pin_1, R5.Pin_1
  N2: Arduino1.A1, R3.pin_1, R6.Pin_1
  N3: Arduino1.A2, R1.pin_1, R4.Pin_1
  N4: Arduino1.D8, SPKR1.pin2
  N5: Arduino1.5V, R1.pin_0, R2.pin_0, R3.pin_0
  GND: Arduino1.GND, R7.Pin_0, R4.Pin_0, R5.Pin_0, R6.Pin_0
  N6: R7.Pin_1, SPKR1.pin1
