# Fritzing sketch LabToneInstrumentNano (saved by Fritzing 0.9.9b)
breadboards: 1

parts:
  R7 = Resistor [tolerance=±5% resistance=100 power=0.25 package=THT]
  SPKR1 = Loudspeaker
  R1 = Basic Force Sensing Resistor (FSR) [package=THT]
  R2 = Basic Force Sensing Resistor (FSR) [package=THT]
  R3 = Basic Force Sensing Resistor (FSR) [package=THT]
  R4 = Resistor [tolerance=±5% resistance=10k power=0.25 package=THT]
  R5 = Resistor [tolerance=±5% resistance=10k power=0.25 package=THT]
  R6 = Resistor [tolerance=±5% resistance=10k power=0.25 package=THT]

nets:
  GND: R7.Pin_0, R4.Pin_0, R5.Pin_0, R6.Pin_0
  N1: R7.Pin_1, SPKR1.pin1
  N2: R1.pin_0, R2.pin_0, R3.pin_0
  N3: R1.pin_1, R4.Pin_1
  N4: R2.pin_1, R5.Pin_1
  N5: R3.pin_1, R6.Pin_1
