# Fritzing sketch LabToneSimpleNano (saved by Fritzing 1.0.5)
breadboards: 1

parts:
  R3 = Resistor [tolerance=±5% resistance=100 power=0.25W package=THT]
  SPKR1 = Loudspeaker
  J1 = Basic Force Sensing Resistor (FSR) [package=THT]
  Part1 = Arduino Nano (Rev3.0)
  R4 = Resistor [tolerance=±5% resistance=10k power=0.25W package=THT]

nets:
  GND: R3.Pin_0, Part1.GND, R4.Pin_0
  N1: R3.Pin_1, SPKR1.pin1
  N2: SPKR1.pin2, Part1.D8
  N3: J1.pin_0, Part1.3V3
  N4: J1.pin_1, Part1.A0, R4.Pin_1
