# Fritzing sketch LabToneTransistor (saved by Fritzing 1.0.5)
breadboards: 1

parts:
  R3 = Resistor [tolerance=±5% resistance=100 power=0.25W package=THT]
  SPKR1 = Loudspeaker
  J1 = Basic Force Sensing Resistor (FSR) [package=THT]
  Part1 = Arduino Nano (Rev3.0)
  R4 = Resistor [tolerance=±5% resistance=10k power=0.25W package=THT]
  Q2 = npn-Powertransistor [package="TO220 [THT]"]

nets:
  GND: R3.Pin_0, Q2.collector
  N1: R3.Pin_1, SPKR1.pin1
  N2: SPKR1.pin2, J1.pin_0, Part1.3V3
  N3: J1.pin_1, R4.Pin_1
  N4: Part1.GND, R4.Pin_0, Q2.base
  N5: Part1.A0, Q2.emitter
