# Fritzing sketch LED_AA_batteries (saved by Fritzing 0.9.9b)
breadboards: 1

parts:
  VCC1 = Battery
  LED1 = smd LED [color="Red (633nm)" package="0603 [SMD]"]
  R1 = Resistor [tolerance=±5% resistance=220 package="2010 [SMD]"]

nets:
  GND: VCC1.-, LED1.cathode
  N1: VCC1.+, R1.Pin_0
  N2: LED1.anode, R1.Pin_1
