# Fritzing sketch Relay (saved by Fritzing 0.9.0b)

parts:
  VCC1 = Battery block 9V
  U1 = RELAY [package=relay-t9a]
  Part1 = Arduino Uno (Rev3)
  LED1 = LED - 5mm [color="Red (633nm)" package="5 mm [THT]"]

nets:
  N1: VCC1.-, U1.NO
  N2: VCC1.+, LED1.anode
  N3: U1.COIL1, Part1.D2
  GND: U1.COIL2, Part1.GND
