# Fritzing sketch h-bridge_schem (saved by Fritzing 0.9.0b)

parts:
  Q2 = Basic FET N-Channel [package="TO220 [THT]"]
  Q4 = Basic FET N-Channel [package="TO220 [THT]"]
  Q1 = Basic FET P-Channel [package="TO220 [THT]"]
  Q3 = Basic FET P-Channel [package="TO220 [THT]"]
  M1 = DC Motor

nets:
  N1: Q2.gate, Q1.gate
  N2: Q2.drain, Q1.source, M1.pin_1
  GND: Q2.source, Q4.source
  N3: Q4.gate, Q3.gate
  N4: Q4.drain, Q3.source, M1.pin_2
  5V: Q1.drain, Q3.drain
