# Fritzing sketch LabAnalogIn (saved by Fritzing 0.9.0b)
breadboards: 1

parts:
  Arduino1 = Arduino Uno (Rev3)
  U1 = POT [package=alps_pot]
  LED1 = LED - 5mm [color="Red (633nm)" package="5 mm [THT]"]
  R1 = Resistor [tolerance=±5% resistance=220 package=THT]

nets:
  N1: Arduino1.A0, U1.S
  N2: Arduino1.D9_PWM, R1.Pin_0
  GND: Arduino1.GND, U1.A, LED1.cathode
  N3: Arduino1.5V, U1.E
  N4: LED1.anode, R1.Pin_1
