# Fritzing sketch LabTwoAnalogIn (saved by Fritzing 0.9.0b)
breadboards: 1

parts:
  Arduino1 = Arduino Uno (Rev3)
  R3 = Basic Force Sensing Resistor (FSR) [package=THT]
  R4 = Basic Force Sensing Resistor (FSR) [package=THT]
  R1 = Resistor [tolerance=±5% resistance=10k package=THT]
  R6 = Resistor [tolerance=±5% resistance=220 package=THT]
  R5 = Resistor [tolerance=±5% resistance=220 package=THT]
  R2 = Resistor [tolerance=±5% resistance=10k package=THT]
  LED1 = LED - 5mm [color="Red (633nm)" package="5 mm [THT]"]
  LED2 = LED - 5mm [color="Green (565nm)" package="5 mm [THT]"]

nets:
  N1: Arduino1.A0, R3.pin_1, R2.Pin_1
  N2: Arduino1.A1, R4.pin_1, R1.Pin_1
  N3: Arduino1.D9_PWM, R6.Pin_0
  N4: Arduino1.D10_PWM/SS, R5.Pin_0
  GND: Arduino1.GND, R1.Pin_0, R2.Pin_0, LED1.cathode, LED2.cathode
  N5: Arduino1.5V, R3.pin_0, R4.pin_0
  N6: R6.Pin_1, LED1.anode
  N7: R5.Pin_1, LED2.anode
