# Fritzing sketch LabDCMotorH-Bridge9VCapacitor (saved by Fritzing 0.9.0b)
breadboards: 1

parts:
  Arduino = Arduino Uno (Rev3)
  R1 = Resistor [tolerance=±5% resistance=10k package=THT]
  M1 = DC Motor
  IC1 = H-Bridge [package=THT]
  VCC1 = Battery block 9V
  C1 = Electrolytic Capacitor [capacitance=100µF package="1010 [SMD, electrolytic]"]
  S1 = Toggle Switch [package=THT]

nets:
  N1: Arduino.D9_PWM, IC1.1_2EN
  N2: Arduino.D2, R1.Pin_1, S1.L2
  N3: Arduino.D3_PWM, IC1.2A
  N4: Arduino.D4, IC1.1A
  N5: Arduino.5V, IC1.VCC1, S1.COM
  GND: Arduino.GND, R1.Pin_0, IC1.GND1, IC1.GND2, IC1.GND3, IC1.GND4, VCC1.-, C1.-
  N6: M1.pin_1, IC1.1Y
  N7: M1.pin_2, IC1.2Y
  N8: IC1.VCC2, VCC1.+, C1.+
