# Fritzing sketch LabElectronicsNoArduino (saved by Fritzing 0.9.0b)
breadboards: 1

parts:
  Power_plug1 = Power plug
  IC1 = Voltage Regulator [package=78xxl]
  S1 = Pushbutton [package="[THT]"]
  R1 = Resistor [tolerance=±5% resistance=220 package=THT]
  LED1 = LED - 5mm [color="Red (633nm)" package="5 mm [THT]"]
  LED2 = LED - 5mm [color="Red (633nm)" package="5 mm [THT]"]

nets:
  N1: Power_plug1.VCC, IC1.IN
  GND: Power_plug1.GND, IC1.GND, LED2.cathode
  N2: IC1.OUT, S1.Pin_3, S1.Pin_4
  N3: S1.Pin_1, S1.Pin_2, R1.Pin_1
  N4: R1.Pin_0, LED1.anode
  N5: LED1.cathode, LED2.anode
