# Fritzing sketch led_potentiometer (saved by Fritzing 0.9.0b)
breadboards: 1

parts:
  Power_plug1 = Power plug
  IC1 = Voltage Regulator [package=78xxl]
  R1 = Resistor [tolerance=±5% resistance=220 package=THT]
  LED1 = LED - 5mm [color="Red (633nm)" package="5 mm [THT]"]
  R2 = POT [package=alps_pot]

nets:
  N1: Power_plug1.VCC, IC1.IN
  GND: Power_plug1.GND, IC1.GND, LED1.cathode, R2.E
  N2: IC1.OUT, R2.A
  N3: R1.Pin_0, LED1.anode
  N4: R1.Pin_1, R2.S
