# Fritzing sketch LabHighCurrentLoadPotentiometer (saved by Fritzing 0.9.0b)
breadboards: 1

parts:
  DC_Motor = DC Motor
  TIP_120_Transistor = npn-Powertransistor [package="TO220 [THT]"]
  Resistor = Resistor [tolerance=±5% resistance=1k package=THT]
  Diode = Rectifier Diode [part_number=1N4001 package="Melf DO-213 AB [SMD]"]
  Potentiometer = POT [package=alps_pot]
  Power_plug = Power plug
  Voltage_Reg = Voltage Regulator [package=78xxl]

nets:
  N1: DC_Motor.pin_1, TIP_120_Transistor.collector, Diode.cathode
  N2: DC_Motor.pin_2, Power_plug.VCC, Voltage_Reg.IN
  N3: TIP_120_Transistor.base, Resistor.Pin_0
  GND: TIP_120_Transistor.emitter, Diode.anode, Potentiometer.A, Power_plug.GND, Voltage_Reg.GND
  N4: Resistor.Pin_1, Potentiometer.S
  N5: Potentiometer.E, Voltage_Reg.OUT
