# Fritzing sketch LabHighCurrentArduinoMotor (saved by Fritzing 0.9.0b)
breadboards: 1

parts:
  Arduino1 = Arduino Uno (Rev3)
  Potentiometer = POT [package=alps_pot]
  TIP_120_Transistor = npn-Powertransistor [package="TO220 [THT]"]
  Motor = DC Motor
  Power_Plug = Power plug
  Diode = Rectifier Diode [part_number=1N4001 package="Melf DO-213 AB [SMD]"]
  Diode_2 = Rectifier Diode [part_number=1N4001 package="300 mil [THT]"]

nets:
  N1: Arduino1.A0, Potentiometer.S
  N2: Arduino1.D9_PWM, TIP_120_Transistor.base
  N3: Arduino1.5V, Potentiometer.E
  GND: Arduino1.GND, Potentiometer.A, TIP_120_Transistor.emitter, Power_Plug.GND, Diode.anode
  N4: TIP_120_Transistor.collector, Motor.pin_2, Diode.cathode, Diode_2.anode
  N5: Motor.pin_1, Power_Plug.VCC, Diode_2.cathode
