# Fritzing sketch LabMidiOut (saved by Fritzing 0.9.0b)
breadboards: 1

parts:
  Arduino1 = Arduino Uno (Rev3)
  DIN1 = DIN-5 jack (MIDI) [package=THT]
  S1 = Pushbutton [package="[THT]"]
  R2 = Resistor [tolerance=±20% resistance=10k package=THT]
  R3 = Resistor [tolerance=±5% resistance=220 package=THT]
  R1 = Resistor [tolerance=±5% resistance=10k package=THT]
  FSR = Basic Force Sensing Resistor (FSR) [package=THT]

nets:
  N1: Arduino1.A0, R1.Pin_1, FSR.pin_0
  N2: Arduino1.D10_PWM/SS, S1.Pin_1, S1.Pin_2, R2.Pin_1
  GND: Arduino1.GND, DIN1.2, R2.Pin_0, R1.Pin_0
  N3: Arduino1.D3_PWM, DIN1.5
  N4: Arduino1.5V, S1.Pin_3, S1.Pin_4, R3.Pin_1, FSR.pin_1
  N5: DIN1.4, R3.Pin_0
