# Fritzing sketch LabSerialIn (saved by Fritzing 0.9.2b)
breadboards: 1

parts:
  Arduino1 = Arduino Uno (Rev3)
  R1 = Resistor [tolerance=±5% resistance=220 package=THT]
  LED1 = LED - 5mm [color="Yellow (592nm)" package="5 mm [THT]"]

nets:
  N1: Arduino1.D11_PWM/MOSI, R1.Pin_0
  GND: Arduino1.GND, LED1.cathode
  N2: R1.Pin_1, LED1.anode
