# Fritzing sketch LabServo (saved by Fritzing 0.9.0b)
breadboards: 1

parts:
  Arduino1 = Arduino Uno (Rev3)
  R2 = Basic Force Sensing Resistor (FSR) [package=THT]
  R1 = Resistor [tolerance=±5% resistance=10k package=THT]
  J1 = Basic Servo

nets:
  N1: Arduino1.A0, R2.pin_1, R1.Pin_1
  GND: Arduino1.GND, R1.Pin_0, J1.gnd
  N2: Arduino1.D3_PWM, J1.pulse
  5V: Arduino1.5V, R2.pin_0, J1.vcc
