# Fritzing sketch LabI2C (saved by Fritzing 0.9.0b)
breadboards: 1

parts:
  Arduino1 = Arduino Uno (Rev3)
  TMP007 = TMP007 Contact-less Infrared Thermopile Sensor

nets:
  N1: Arduino1.A4/SDA, TMP007.SCL
  N2: Arduino1.A5/SCL, TMP007.ALERT
  5V: Arduino1.5V, TMP007.VCC
  GND: Arduino1.GND, TMP007.GND

custom parts:
  TMP007 Contact-less Infrared Thermopile Sensor: The TMP007 is an infrared (IR) thermopile sensor that measures the temperature of an object without contacting the object. The integrated thermopile absorbs the infrared energy emitted from the object in the sensor field of view. The thermopile voltage is digitized and provided as an input to the integrated math engine, along with the die temperature. The math engine then computes the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
