# Fritzing sketch LabToneSimple (saved by Fritzing 0.9.0b)
breadboards: 1

parts:
  Arduino1 = Arduino Uno (Rev3)
  R1 = Photocell (LDR) [package=THT]
  R2 = Photocell (LDR) [package=THT]
  R3 = Resistor [tolerance=±5% resistance=100 package=THT]
  SPKR1 = Loudspeaker

nets:
  N1: Arduino1.A0, R1.pin_0, R2.pin_1
  N2: Arduino1.D8, SPKR1.pin2
  N3: Arduino1.5V, R1.pin_1
  GND: Arduino1.GND, R2.pin_0, R3.Pin_0
  N4: R3.Pin_1, SPKR1.pin1
