# Fritzing sketch level_shifting_uno_to_pi (saved by Fritzing 0.9.3b)

parts:
  Part1 = Arduino Uno (Rev3) - ICSP
  BB1 = 8-Line Bi-Directional Level Shifter
  Raspberry_Pi_1 = Raspberry Pi 3 [part_number=RPI-3-V1.2]

nets:
  GND: Part1.GND, BB1.no_name_yet#20, Raspberry_Pi_1.GND
  N1: Part1.D0/RX, BB1.no_name_yet#12
  N2: Part1.D1/TX, BB1.no_name_yet#13
  N3: Part1.5V, BB1.no_name_yet#11
  3V3: BB1.no_name_yet#1, Raspberry_Pi_1.3v3, Raspberry_Pi_1.5V
  N4: BB1.no_name_yet#2, Raspberry_Pi_1.GIPO14
  N5: BB1.no_name_yet#3, Raspberry_Pi_1.GIPO15

custom parts:
  8-Line Bi-Directional Level Shifter: 8-channel Bi-Directional Level Shifter with TXB0108
