# Fritzing sketch Electricity lab (saved by Fritzing 0.6.2b)
breadboards: 1

parts:
  Voltage_Regulator = Voltage Regulator - 5V [package="TO220 [THT]"]
  Power_plug1 = Power plug
  LED1 = Red LED - 5mm
  220_ohm = Resistor [resistance=560 tolerance=±5% package=THT]

nets:
  N1: Voltage_Regulator.input_voltage, Power_plug1.VCC
  GND: Voltage_Regulator.GND, Power_plug1.GND, LED1.cathode
  N2: Voltage_Regulator.output_voltage, 220_ohm.Pin_0
  N3: LED1.anode, 220_ohm.Pin_1
