# Fritzing sketch Electricity lab3 (saved by Fritzing 0.3.14b)
breadboards: 1

parts:
  Voltage_Regulator = Voltage Regulator - 5V [package="TO220 [THT]"]
  Power_plug1 = Power plug
  LED1 = Red LED - 5mm
  220_ohm = Resistor [resistance=220 package=THT]
  S1 = Pushbutton [package="[THT]"]
  LED1_2 = Red LED - 5mm

nets:
  N1: Voltage_Regulator.input_voltage, Power_plug1.VCC
  GND: Voltage_Regulator.GND, Power_plug1.GND, LED1_2.cathode
  N2: Voltage_Regulator.output_voltage, S1.Pin_3, S1.Pin_4
  N3: LED1.cathode, LED1_2.anode
  N4: LED1.anode, 220_ohm.Pin_0
  N5: 220_ohm.Pin_1, S1.Pin_1, S1.Pin_2
