# Fritzing sketch Electricity lab3 (saved by Fritzing 0.8.7b)
breadboards: 1

parts:
  Voltage_Regulator = Voltage Regulator - 5V [package="TO220 [THT]"]
  S1 = Pushbutton [package="[THT]"]
  part = Power plug  # not connected
  LED1 = LED - 5mm [color="Red (633nm)" package="5 mm [THT]"]
  LED1_2 = LED - 5mm [color="Red (633nm)" package="5 mm [THT]"]
  Power_plug1 = Power plug
  R1 = Resistor [tolerance=±5% resistance=220 package=THT]

nets:
  N1: Voltage_Regulator.input_voltage, Power_plug1.VCC
  GND: Voltage_Regulator.GND, LED1_2.cathode, Power_plug1.GND
  N2: Voltage_Regulator.output_voltage, S1.Pin_3, S1.Pin_4
  N3: S1.Pin_1, S1.Pin_2, R1.Pin_1
  N4: LED1.cathode, LED1_2.anode
  N5: LED1.anode, R1.Pin_0
