# Fritzing sketch Electricity lab2 (saved by Fritzing 0.6.2b)
breadboards: 1

parts:
  Voltage_Regulator = Voltage Regulator - 5V [package="TO220 [THT]"]
  LED1 = Red LED - 5mm
  220_ohm = Resistor [resistance=560 tolerance=±5% package=THT]
  R1 = Rotary Potentiometer (Large) [package=THT]
  Power_plug1 = Power plug

nets:
  N1: Voltage_Regulator.input_voltage, Power_plug1.VCC
  GND: Voltage_Regulator.GND, LED1.cathode, R1.leg1, Power_plug1.GND
  N2: Voltage_Regulator.output_voltage, R1.leg2
  N3: LED1.anode, 220_ohm.Pin_0
  N4: 220_ohm.Pin_1, R1.wiper
