# Fritzing sketch MouseLabPhotocell (saved by Fritzing 0.8.0b)
breadboards: 1

parts:
  Leonardo = Arduino Leonardo (Rev3b)
  R4 = Photocell (LDR) [package=THT]
  R5 = Photocell (LDR) [package=THT]
  R3 = Resistor [tolerance=±5% resistance=10k package=THT]
  R2 = Resistor [tolerance=±5% resistance=10k package=THT]
  R1 = Resistor [tolerance=±5% resistance=10k package=THT]
  S1 = Pushbutton [package="[SMD]"]

nets:
  N1: Leonardo.D2/SDA, R1.Pin_1, S1.Pin_3, S1.Pin_4
  N2: Leonardo.5V, R4.pin_1, R5.pin_1, S1.Pin_1, S1.Pin_2
  N3: Leonardo.GND, R3.Pin_1, R2.Pin_0, R1.Pin_0
  N4: Leonardo.A0, R5.pin_0, R3.Pin_0
  N5: Leonardo.A1, R4.pin_0, R2.Pin_1
