# Fritzing sketch MouseLabButtons (saved by Fritzing 0.8.0b)
breadboards: 1

parts:
  Leonardo = Arduino Leonardo (Rev3b)
  R3 = Resistor [tolerance=±5% resistance=10k package=THT]
  R4 = Resistor [tolerance=±5% resistance=10k package=THT]
  S1 = Pushbutton [package="[SMD]"]
  S5 = Pushbutton [package="[THT]"]
  S3 = Pushbutton [package="[THT]"]
  S4 = Pushbutton [package="[THT]"]
  S2 = Pushbutton [package="[THT]"]
  R2 = Resistor [tolerance=±5% resistance=10k package=THT]
  R1 = Resistor [tolerance=±5% resistance=10k package=THT]
  R5 = Resistor [tolerance=±5% resistance=10k package=THT]

nets:
  N1: Leonardo.D2/SDA, S1.Pin_3, S1.Pin_4, R1.Pin_0
  N2: Leonardo.D3_PWM/SCL, S2.Pin_3, S2.Pin_4, R2.Pin_1
  N3: Leonardo.D4/A6, R3.Pin_1, S3.Pin_3, S3.Pin_4
  N4: Leonardo.D5_PWM, R4.Pin_0, S4.Pin_3, S4.Pin_4
  N5: Leonardo.D6_PWM/A7, S5.Pin_3, S5.Pin_4, R5.Pin_0
  N6: Leonardo.5V, S1.Pin_1, S1.Pin_2, S5.Pin_1, S5.Pin_2, S3.Pin_1, S3.Pin_2, S4.Pin_1, S4.Pin_2, S2.Pin_1, S2.Pin_2
  N7: Leonardo.GND, R3.Pin_0, R4.Pin_1, R2.Pin_0, R1.Pin_1, R5.Pin_1
