# Fritzing sketch Servo_analog_sensor (saved by Fritzing 0.6.2b)
breadboards: 1

parts:
  Arduino2 = Arduino Uno
  R1 = Basic Force Sensing Resistor (FSR) [package=THT]
  R2 = Resistor [tolerance=±5% resistance=10k package=THT]
  S1 = Basic Servo

nets:
  N1: Arduino2.connector13, S1.pulse
  N2: Arduino2.connector18, R1.pin_0, S1.vcc
  GND: Arduino2.connector19, R2.Pin_0, S1.gnd
  N3: Arduino2.connector23, R1.pin_1, R2.Pin_1
