# Fritzing sketch UnipolarStepperLab (saved by Fritzing 0.9.0b)
breadboards: 1

parts:
  H-Bridge = L293D [package=THT]
  Unipolar_Stepper = Adafruit Gear-Reduced Stepper Motor (small)
  12V_Power_supply = 2.1mm Barrel Jack with Terminal Block
  Arduino = Arduino Uno (Rev3)

nets:
  5V: H-Bridge.Enable_1, H-Bridge.Enable_2, H-Bridge.+V, Arduino.5V
  N1: H-Bridge.In_1, Arduino.D8
  Motor pin B: H-Bridge.Out_1_(_Controlled_by_Enable_1_), Unipolar_Stepper.PINK
  GND: H-Bridge.0V, 12V_Power_supply.NEG, Arduino.GND
  Motor pin D: H-Bridge.Out_2_(_Controlled_by_Enable_1_), Unipolar_Stepper.ORANGE
  N2: H-Bridge.In_2, Arduino.D9_PWM
  12V: H-Bridge.+Vmotor, Unipolar_Stepper.RED, 12V_Power_supply.POS
  N3: H-Bridge.In_3, Arduino.D10_PWM/SS
  N4: H-Bridge.Out_3_(_Controlled_by_Enable_2_), Unipolar_Stepper.YELLOW
  N5: H-Bridge.Out_4_(_Controlled_by_Enable_2_), Unipolar_Stepper.BLUE
  N6: H-Bridge.In_4, Arduino.D11_PWM/MOSI

custom parts:
  Adafruit Gear-Reduced Stepper Motor (small): Adafruit gear-reduction stepper motor (small)
