# Fritzing sketch UnipolarStepperLabTwoWire (saved by Fritzing 0.9.0b)
breadboards: 1

parts:
  H-Bridge = L293D [package=THT]
  12V_Power_supply = 2.1mm Barrel Jack with Terminal Block
  part = 2.1mm Barrel Jack with Terminal Block  # not connected
  Arduino = Arduino Uno (Rev3)
  Q1 = NPN-Transistor [package="TO92 [THT]"]
  Q2 = NPN-Transistor [package="TO92 [THT]"]
  R1 = Resistor [tolerance=±5% resistance=1k package=THT]
  R2 = Resistor [tolerance=±5% resistance=10k package=THT]
  R3 = Resistor [tolerance=±5% resistance=1k package=THT]
  R4 = Resistor [tolerance=±5% resistance=10k package=THT]
  MOTOR1 = Adafruit Gear-Reduced Stepper Motor (small)

nets (from the schematic view):
  5V: H-Bridge.Enable_1, H-Bridge.Enable_2, H-Bridge.+V, Arduino.5V, R2.Pin_0, R4.Pin_1
  N1: H-Bridge.In_1, Arduino.D8, R1.Pin_1
  Motor wire B: H-Bridge.Out_1_(_Controlled_by_Enable_1_), MOTOR1.PINK
  GND: H-Bridge.0V, 12V_Power_supply.NEG, Arduino.GND, Q1.E, Q2.E
  Motor wire D: H-Bridge.Out_2_(_Controlled_by_Enable_1_), MOTOR1.ORANGE
  N2: H-Bridge.In_2, Q1.C, R2.Pin_1
  12V: H-Bridge.+Vmotor, 12V_Power_supply.POS, MOTOR1.RED
  N3: H-Bridge.In_3, Q2.C, R4.Pin_0
  N4: H-Bridge.Out_3_(_Controlled_by_Enable_2_), MOTOR1.BLUE
  N5: H-Bridge.Out_4_(_Controlled_by_Enable_2_), MOTOR1.YELLOW
  H-bridge control 2: H-Bridge.In_4, Arduino.D9_PWM, R3.Pin_1
  N6: Q1.B, R1.Pin_0
  N7: Q2.B, R3.Pin_0

custom parts:
  Adafruit Gear-Reduced Stepper Motor (small): Adafruit gear-reduction stepper motor (small)
