# Fritzing sketch Switch_LED (saved by Fritzing 0.8.0b)
breadboards: 1

parts:
  Power_plug = Power plug
  Switch = Pushbutton [package="[THT]"]
  5V_Voltage_Regulator = Voltage Regulator - 5V [package="TO220 [THT]"]
  Resistor = Resistor [tolerance=±0.05% resistance=220 package=THT]
  LED1 = LED - 5mm [color="Red (633nm)" package="5 mm [THT]"]

nets:
  GND: Power_plug.GND, 5V_Voltage_Regulator.GND, LED1.cathode
  N1: Power_plug.VCC, 5V_Voltage_Regulator.input_voltage
  N2: Switch.Pin_1, Switch.Pin_2, Resistor.Pin_1
  N3: Switch.Pin_4, 5V_Voltage_Regulator.output_voltage
  N4: Resistor.Pin_0, LED1.anode
