# Fritzing sketch Tone lab 2 (saved by Fritzing 0.6.2b)
breadboards: 1

parts:
  SPKR1 = Loudspeaker
  FSR1 = Basic Force Sensing Resistor (FSR) [package=THT]
  FSR2 = Basic Force Sensing Resistor (FSR) [package=THT]
  FSR3 = Basic Force Sensing Resistor (FSR) [package=THT]
  R3 = Resistor [resistance=10k tolerance=±5% package=THT]
  R2 = Resistor [resistance=10k tolerance=±5% package=THT]
  R1 = Resistor [resistance=10k tolerance=±5% package=THT]
  Arduino3 = Arduino Uno
  R4 = Resistor [tolerance=±5% resistance=100 package=THT]

nets (from the breadboard view):
  N1: SPKR1.pin1, R3.Pin_0, R2.Pin_0, R1.Pin_0, Arduino3.connector19
  N2: SPKR1.pin2, R4.Pin_1
  N3: FSR1.pin_0, FSR2.pin_0, FSR3.pin_0, Arduino3.connector18
  N4: FSR1.pin_1, R1.Pin_1, Arduino3.connector24
  N5: FSR2.pin_1, R2.Pin_1, Arduino3.connector23
  N6: FSR3.pin_1, R3.Pin_1, Arduino3.connector22
  N7: Arduino3.connector7, R4.Pin_0
