# Fritzing sketch Tone lab 3 (saved by Fritzing 0.3.14b)

parts:
  Arduino1 = Arduino
  SPKR1 = Loudspeaker
  R1 = Resistor [resistance=100 package=THT]

nets:
  N1: Arduino1.GND, SPKR1.pin1
  N2: Arduino1.D8, R1.Pin_0
  N3: SPKR1.pin2, R1.Pin_1
