# Fritzing sketch Tone lab 4 (saved by Fritzing 0.3.14b)

parts:
  Arduino1 = Arduino
  speaker = Loudspeaker
  100Ω = Resistor [resistance=100 package=THT]
  speaker_2 = Loudspeaker
  100Ω_2 = Resistor [resistance=100 package=THT]
  speaker_3 = Loudspeaker
  100Ω_3 = Resistor [resistance=100 package=THT]

nets:
  N1: Arduino1.GND, speaker.pin1, speaker_2.pin1, speaker_3.pin1
  N2: Arduino1.D8, 100Ω.Pin_0
  N3: Arduino1.D7, 100Ω_2.Pin_0
  N4: Arduino1.D6, 100Ω_3.Pin_0
  N5: speaker.pin2, 100Ω.Pin_1
  N6: speaker_2.pin2, 100Ω_3.Pin_1
  N7: 100Ω_2.Pin_1, speaker_3.pin2
