# Fritzing sketch Lamp_Lab (saved by Fritzing 0.8.3b)
breadboards: 1

parts:
  5V_Voltage_Regulator = Voltage Regulator - 5V [package="TO220 [THT]"]
  Power_plug = Power plug
  Resistor = Resistor [tolerance=±5% resistance=1k package=THT]
  Switch = Pushbutton [package=THT]
  Transistor = Basic FET N-Channel [package="TO220 [THT]"]
  LED1 = LED - 5mm [color="Red (633nm)" package="5 mm [THT]"]

nets:
  N1: 5V_Voltage_Regulator.input_voltage, Power_plug.VCC, LED1.anode
  GND: 5V_Voltage_Regulator.GND, Power_plug.GND, Transistor.source
  N2: 5V_Voltage_Regulator.output_voltage, Switch.leg1
  N3: Resistor.Pin_0, Transistor.gate
  N4: Resistor.Pin_1, Switch.leg0
  N5: Transistor.drain, LED1.cathode
