# Fritzing sketch VoltageReg (saved by Fritzing 0.8.3b)
breadboards: 1

parts:
  5V_Voltage_Regulator = Voltage Regulator - 5V [package="TO220 [THT]"]
  Power_plug = Power plug

nets:
  N1: 5V_Voltage_Regulator.input_voltage, Power_plug.VCC
  GND: 5V_Voltage_Regulator.GND, Power_plug.GND
