# Fritzing sketch TransistorLab (saved by Fritzing 0.6.3b)
breadboards: 1

parts:
  Arduino2 = Arduino Uno
  Q1 = Basic FET N-Channel [package="TO220 [THT]"]
  R1 = Rotary Potentiometer (Large) [maximum_resistance=100kΩ package=THT]
  LED1 = LED - 5mm [color="Red (633nm)" package="5 mm [THT]"]

nets:
  N1: Arduino2.connector7, Q1.gate
  N2: Arduino2.connector18, R1.leg1
  N3: Arduino2.connector19, Q1.source, R1.leg2
  GND: Arduino2.connector20
  N4: Arduino2.connector22, R1.wiper
  N5: Q1.drain, LED1.cathode
