# Fritzing sketch Motor_Lab_noswitchnodiode (saved by Fritzing 0.8.3b)
breadboards: 1

parts:
  Motor = DC Motor
  5V_Voltage_Regulator = Voltage Regulator - 5V [package="TO220 [THT]"]
  Power_plug = Power plug
  Resistor = Resistor [tolerance=±5% resistance=1k package=THT]
  Transistor = Basic FET N-Channel [package="TO220 [THT]"]

nets:
  N1: Motor.pin_1, Transistor.drain
  N2: Motor.pin_2, 5V_Voltage_Regulator.input_voltage, Power_plug.VCC
  GND: 5V_Voltage_Regulator.GND, Power_plug.GND, Transistor.source
  N3: 5V_Voltage_Regulator.output_voltage, Resistor.Pin_1
  N4: Resistor.Pin_0, Transistor.gate
