# Fritzing sketch TransistorLab (saved by Fritzing 0.8.0b)
breadboards: 1

parts:
  Arduino = Arduino Uno (Rev3)
  R1 = Rotary Potentiometer (Large) [maximum_resistance=100kΩ package=THT]
  Q1 = Basic FET N-Channel [package="TO220 [THT]"]
  M1 = DC Motor
  JACK1 = 2.1mm Barrel Jack with Terminal Block
  D1 = Rectifier Diode [part_number=1N4001 package="300 mil [THT]"]

nets:
  N1: Arduino.A0, R1.wiper
  GND: Arduino.GND, R1.leg2, Q1.source, JACK1.NEG, D1.anode
  N2: Arduino.D8, Q1.gate
  N3: Arduino.5V, R1.leg1
  N4: Q1.drain, M1.pin_2, D1.cathode
  N5: M1.pin_1, JACK1.POS
