# Fritzing sketch Class2_DCMotor_no_LED (saved by Fritzing 0.8.3b)
breadboards: 1

parts:
  Power_plug = Power plug
  Switch = Pushbutton [package="[THT]"]
  5V_Voltage_Regulator = Voltage Regulator - 5V [package="TO220 [THT]"]
  DC_Motor = DC Motor

nets:
  GND: Power_plug.GND, 5V_Voltage_Regulator.GND, DC_Motor.pin_2
  N1: Power_plug.VCC, 5V_Voltage_Regulator.input_voltage
  N2: Switch.Pin_2, DC_Motor.pin_1
  N3: Switch.Pin_3, Switch.Pin_4, 5V_Voltage_Regulator.output_voltage
