# Fritzing sketch Motor_Lab_VDiv (saved by Fritzing 0.8.3b)
breadboards: 1

parts:
  Motor = DC Motor
  5V_Voltage_Regulator = Voltage Regulator - 5V [package="TO220 [THT]"]
  Power_plug = Power plug
  Diode = Rectifier Diode [part_number=1N4001 package="300 mil [THT]"]
  Transistor = Basic FET N-Channel [package="TO220 [THT]"]
  Variable_Res = Photocell (LDR) [package=THT]
  Fixed_Res = Resistor [tolerance=±5% resistance=220 package=THT]

nets:
  N1: Motor.pin_1, Diode.cathode, Transistor.drain
  N2: Motor.pin_2, 5V_Voltage_Regulator.input_voltage, Power_plug.VCC
  GND: 5V_Voltage_Regulator.GND, Power_plug.GND, Diode.anode, Transistor.source, Fixed_Res.Pin_1
  N3: 5V_Voltage_Regulator.output_voltage, Variable_Res.pin_0
  N4: Transistor.gate, Variable_Res.pin_1, Fixed_Res.Pin_0
