# Fritzing sketch DigitalInOut (saved by Fritzing 0.6.3b)
breadboards: 1

parts:
  Arduino = Arduino Uno
  S1 = Pushbutton [package="[THT]"]
  LED2 = Red LED - 5mm [package="5 mm [THT]"]
  LED1 = yellow LED - 5mm [package="5 mm [THT]"]
  R2 = Resistor [tolerance=±5% resistance=560 package=THT]
  R1 = Resistor [tolerance=±5% resistance=10k package=THT]
  R3 = Resistor [tolerance=±5% resistance=560 package=THT]

nets:
  GND: Arduino.connector1, Arduino.connector19, LED2.cathode, LED1.cathode, R1.Pin_0
  N1: Arduino.connector11, R3.Pin_0
  N2: Arduino.connector12, R2.Pin_0
  N3: Arduino.connector13, S1.Pin_1, S1.Pin_2, R1.Pin_1
  N4: Arduino.connector18, S1.Pin_3, S1.Pin_4
  N5: LED2.anode, R3.Pin_1
  N6: LED1.anode, R2.Pin_1
