# Fritzing sketch AnalogInOut2 (saved by Fritzing 0.6.2b)
breadboards: 1

parts:
  Arduino1 = Arduino Uno
  LED1 = Red LED - 5mm [package="5 mm [THT]"]
  R2 = Resistor [tolerance=±5% resistance=560 package=THT]
  J1 = Basic Force Sensing Resistor (FSR) [package=THT]
  R4 = Resistor [tolerance=±5% resistance=10k package=THT]
  R5 = Resistor [tolerance=±5% resistance=10k package=THT]
  J2 = Basic Force Sensing Resistor (FSR) [package=THT]
  LED2 = green LED - 5mm [package="5 mm [THT]"]
  R7 = Resistor [tolerance=±5% resistance=560 package=THT]

nets:
  GND: Arduino1.connector1, Arduino1.connector19, LED1.cathode, R4.Pin_0, R5.Pin_0, LED2.cathode
  N1: Arduino1.connector4, R7.Pin_0
  N2: Arduino1.connector5, R2.Pin_0
  N3: Arduino1.connector18, J1.pin_0, J2.pin_0
  N4: Arduino1.connector22, R5.Pin_1, J2.pin_1
  N5: Arduino1.connector23, J1.pin_1, R4.Pin_1
  N6: LED1.anode, R2.Pin_1
  N7: LED2.anode, R7.Pin_1
