# Fritzing sketch Tone lab (saved by Fritzing 0.6.2b)
breadboards: 1

parts:
  SPKR1 = Loudspeaker
  Photocell = Photocell (LDR) [package=THT]
  Arduino3 = Arduino Uno
  Photocell1 = Photocell (LDR) [package=THT]
  R3 = Resistor [tolerance=±5% resistance=100 package=THT]

nets:
  N1: SPKR1.pin1, R3.Pin_0
  N2: SPKR1.pin2, Arduino3.connector7
  N3: Photocell.pin_0, Arduino3.connector23, Photocell1.pin_0
  N4: Photocell.pin_1, Arduino3.connector18
  N5: Arduino3.connector19, Photocell1.pin_1, R3.Pin_1
