# Fritzing sketch XbeeSerialConnection (saved by Fritzing 0.3.16b)

parts:
  U1 = XBee
  Arduino1 = Arduino
  Arduino1_2 = Arduino
  U1_2 = XBee

nets:
  VCC: U1.VCC, Arduino1.3V3
  N1: U1.pin2, Arduino1.D0RX
  N2: U1.pin3, Arduino1.D1TX
  GND: U1.GND, Arduino1.GND
  GND_2: Arduino1_2.GND, U1_2.GND
  N3: Arduino1_2.D1TX, U1_2.pin3
  N4: Arduino1_2.D0RX, U1_2.pin2
  3V3: Arduino1_2.3V3, U1_2.VCC
