# Fritzing sketch AnalogInOut (saved by Fritzing 0.4.2b)
breadboards: 1

parts:
  Arduino1 = Arduino
  R1 = Rotary Potentiometer (Large) [package=THT]
  LED1 = Red LED - 5mm
  R2 = Resistor [resistance=220 package=THT]

nets:
  N1: Arduino1.GND, R1.leg1, LED1.cathode
  N2: Arduino1.D9, R2.Pin_0
  N3: Arduino1.+5V, R1.leg2
  N4: Arduino1.A0, R1.wiper
  N5: LED1.anode, R2.Pin_1
