# Fritzing sketch DigitalInOut2 (saved by Fritzing 0.9.0b)
breadboards: 1

parts:
  S1 = Pushbutton [package="[THT]"]
  R2 = Resistor [tolerance=±5% resistance=560 package=THT]
  R3 = Resistor [tolerance=±5% resistance=560 package=THT]
  part = Resistor [tolerance=±5% resistance=220 package=THT]  # not connected
  LED1 = LED - 5mm [color="Yellow (585nm)" package="5 mm [THT]"]
  LED2 = LED - 5mm [color="Red (633nm)" package="5 mm [THT]"]
  Part1 = Arduino Uno (Rev3)
  R1 = Resistor [tolerance=±5% resistance=10k package=THT]

nets:
  N1: S1.Pin_1, S1.Pin_2, Part1.D2, R1.Pin_1
  N2: S1.Pin_3, S1.Pin_4, Part1.5V
  N3: R2.Pin_0, Part1.D3_PWM
  N4: R2.Pin_1, LED1.anode
  N5: R3.Pin_0, Part1.D4
  N6: R3.Pin_1, LED2.anode
  GND: LED1.cathode, LED2.cathode, Part1.GND, R1.Pin_0
  12V: Part1.VIN
