# Fritzing sketch hBridge (saved by Fritzing 0.6.3b)
breadboards: 1

parts:
  Arduino1 = Arduino Uno
  IC1 = H-Bridge [package=THT]
  R1 = Resistor [tolerance=±5% resistance=10k package=THT]
  M1 = DC Motor
  VCC1 = Battery block 9V
  S1 = Pushbutton [package=THT]
  C1 = Electrolytic Capacitor [capacitance=1µF package="100 mil [THT, electrolytic]"]

nets:
  GND: Arduino1.connector1, Arduino1.connector13, Arduino1.connector19, IC1.GND1, IC1.GND2, IC1.GND3, IC1.GND4, R1.Pin_0, R1.Pin_1, VCC1.-, S1.leg1
  N1: Arduino1.connector6, IC1.1_2EN
  N2: Arduino1.connector11, IC1.1A
  N3: Arduino1.connector12, IC1.2A
  N4: Arduino1.connector18, IC1.VCC1, S1.leg0
  N5: IC1.1Y, M1.pin_1
  N6: IC1.2Y, M1.pin_2
  N7: IC1.VCC2, VCC1.+, C1.-
