# Fritzing sketch KeyboardLabButtons (saved by Fritzing 0.9.3b)
breadboards: 1

parts:
  R3 = Resistor [tolerance=±5% resistance=10k package=THT]
  R4 = Resistor [tolerance=±5% resistance=10k package=THT]
  S1 = Pushbutton [package="[SMD]"]
  S5 = Pushbutton [package="[THT]"]
  S3 = Pushbutton [package="[THT]"]
  S4 = Pushbutton [package="[THT]"]
  S2 = Pushbutton [package="[THT]"]
  R2 = Resistor [tolerance=±5% resistance=10k package=THT]
  R1 = Resistor [tolerance=±5% resistance=10k package=THT]
  part = Resistor [tolerance=±5% resistance=220 package=THT]  # not connected
  LED1 = LED - 5mm [color="Green (565nm)" package="5 mm [THT]"]
  R6 = Resistor [tolerance=±5% resistance=220 package=THT]
  Leonardo = Arduino Leonardo (Rev3b)
  R5 = Resistor [tolerance=±5% resistance=10k package=THT]

nets:
  N1: R3.Pin_0, R4.Pin_1, R2.Pin_0, R1.Pin_1, LED1.cathode, Leonardo.GND, R5.Pin_1
  N2: R3.Pin_1, S3.Pin_3, S3.Pin_4, Leonardo.D4/A6
  N3: R4.Pin_0, S4.Pin_3, S4.Pin_4, Leonardo.D5_PWM
  N4: S1.Pin_1, S1.Pin_2, S5.Pin_1, S5.Pin_2, S3.Pin_1, S3.Pin_2, S4.Pin_1, S4.Pin_2, S2.Pin_1, S2.Pin_2, Leonardo.5V
  N5: S1.Pin_3, S1.Pin_4, R1.Pin_0, Leonardo.D2/SDA
  N6: S5.Pin_3, S5.Pin_4, Leonardo.D6_PWM/A7, R5.Pin_0
  N7: S2.Pin_3, S2.Pin_4, R2.Pin_1, Leonardo.D3_PWM/SCL
  N8: LED1.anode, R6.Pin_1
  N9: R6.Pin_0, Leonardo.D13_PWM
