# Fritzing sketch digital_in_pullup (saved by Fritzing 0.8.3b)
breadboards: 1

parts:
  R1_Pullup_resistor = Resistor [tolerance=±5% resistance=10k package=THT]
  S1 = Pushbutton [package="[THT]"]

nets:
  5V: R1_Pullup_resistor.Pin_0
  N1: R1_Pullup_resistor.Pin_1, S1.Pin_3, S1.Pin_4
  GND: S1.Pin_2

notes:
  To Digital Input
