# Fritzing sketch Servo_analog_sensor (saved by Fritzing 0.8.0b)
breadboards: 1

parts:
  R1 = Basic Force Sensing Resistor (FSR) [package=THT]
  R2 = Resistor [tolerance=±5% resistance=10k package=THT]
  S1 = Basic Servo
  Arduino_Uno = Arduino Uno (Rev3)

nets:
  VCC: R1.pin_0, S1.vcc, Arduino_Uno.5V
  N1: R1.pin_1, R2.Pin_1, Arduino_Uno.A0
  GND: R2.Pin_0, S1.gnd, Arduino_Uno.GND
  N2: S1.pulse, Arduino_Uno.D2
