# Fritzing sketch Switchlab2 (saved by Fritzing 0.3.14b)
breadboards: 1

parts:
  Voltage_Regulator = Voltage Regulator - 5V [package="TO220 [THT]"]
  Power_plug1 = Power plug
  220_ohm = Resistor [resistance=220 package=THT]
  S1 = Pushbutton [package="[THT]"]
  LED1 = Red LED - 5mm
  S3 = Pushbutton [package="[THT]"]
  S3_2 = Pushbutton [package="[THT]"]

nets:
  N1: Voltage_Regulator.input_voltage, Power_plug1.VCC
  GND: Voltage_Regulator.GND, Power_plug1.GND, 220_ohm.Pin_1
  N2: Voltage_Regulator.output_voltage, LED1.cathode
  N3: 220_ohm.Pin_0, S1.Pin_3, S1.Pin_4
  N4: S1.Pin_1, S1.Pin_2, S3_2.Pin_3, S3_2.Pin_4
  N5: LED1.anode, S3.Pin_1, S3.Pin_2
  N6: S3.Pin_3, S3.Pin_4, S3_2.Pin_1, S3_2.Pin_2
