# Fritzing sketch TransistorAlternate (saved by Fritzing 0.8.3b)
breadboards: 1

parts:
  Q3 = Basic FET N-Channel [package="TO220 [THT]"]
  U1 = Voltage Regulator - 5V [package="DPak [SMD]"]
  M1 = DC Motor  # not connected
  Q1 = npn-Powertransistor [part_number=TIP120 package="TO220 [THT]"]
  part = Resistor [tolerance=±5% resistance=1k package=THT]
  M2 = DC Motor
  R2 = Resistor [tolerance=±5% resistance=1k package=THT]
  Q4 = npn-Powertransistor [part_number=TIP120 package="TO220 [THT]"]
  M3 = DC Motor
  D6 = Rectifier Diode [part_number=1N4001 package="300 mil [THT]"]
  R5 = Rotary Potentiometer (Small)
  Q5 = npn-Powertransistor [part_number=TIP120 package="TO220 [THT]"]
  M4 = DC Motor
  D7 = Rectifier Diode [part_number=1N4001 package="300 mil [THT]"]
  R6 = Photocell (LDR) [package=THT]
  R7 = Resistor [package="2010 [SMD]"]

nets:
  N1: Q3.gate, R2.Pin_0
  N2: Q3.drain, M2.pin_1
  GND: Q3.source, U1.GND, Q1.emitter, Q4.emitter, R5.leg1, Q5.emitter, R7.Pin_1
  12V: U1.input_voltage
  5V: U1.output_voltage, part.Pin_1, R2.Pin_1, R5.leg2, R6.pin_0
  N3: Q1.base, part.Pin_0
  N4: Q4.base, R5.wiper
  N5: M3.pin_1, D6.anode
  N6: M3.pin_2, D6.cathode
  N7: Q5.base, R6.pin_1, R7.Pin_0
  N8: M4.pin_1, D7.anode
  N9: M4.pin_2, D7.cathode
