# Fritzing sketch Class2_Transistor (saved by Fritzing 0.4.3b)
breadboards: 1

parts:
  Power_plug1 = Power plug
  S1 = Pushbutton [package="[THT]"]
  U1 = Voltage Regulator - 5V [package="TO220 [THT]"]
  R1 = Resistor [resistance=220 package=THT]
  LED1 = Red LED - 5mm
  M1 = DC Motor

nets:
  GND: Power_plug1.GND, U1.GND, LED1.cathode, LED1.anode, M1.pin_2
  N1: Power_plug1.VCC, U1.input_voltage
  N2: S1.Pin_1, S1.Pin_2, U1.output_voltage
  N3: S1.Pin_3, S1.Pin_4, R1.Pin_0, M1.pin_1
