# Fritzing sketch Motor_Lab (saved by Fritzing 0.8.0b)
breadboards: 1

parts:
  M1 = DC Motor
  Q1 = Basic FET N-Channel [package="TO220 [THT]"]
  LED1 = LED - 5mm [color="Red (633nm)" package="5 mm [THT]"]
  R1 = Resistor [tolerance=±5% resistance=220 package=THT]
  U1 = Voltage Regulator - 5V [package="TO220 [THT]"]
  Power_plug1 = Power plug
  R4 = Resistor [tolerance=±5% resistance=1k package=THT]
  S1 = Pushbutton [package=THT]

nets:
  N1: M1.pin_1, Q1.drain
  N2: M1.pin_2, U1.input_voltage, Power_plug1.VCC
  N3: Q1.gate, R4.Pin_0
  GND: Q1.source, LED1.cathode, U1.GND, Power_plug1.GND
  N4: LED1.anode, R1.Pin_1
  N5: R1.Pin_0, R4.Pin_1, S1.leg0
  N6: U1.output_voltage, S1.leg1
