# Fritzing sketch Motor_Lab_Pot_nores (saved by Fritzing 0.8.3b)
breadboards: 1

parts:
  Motor = DC Motor
  5V_Voltage_Regulator = Voltage Regulator - 5V [package="TO220 [THT]"]
  Power_plug = Power plug
  Diode = Rectifier Diode [part_number=1N4001 package="300 mil [THT]"]
  Transistor = Basic FET N-Channel [package="TO220 [THT]"]
  R1 = Rotary Potentiometer (Small)

nets:
  N1: Motor.pin_1, Diode.cathode, Transistor.drain
  N2: Motor.pin_2, 5V_Voltage_Regulator.input_voltage, Power_plug.VCC
  GND: 5V_Voltage_Regulator.GND, Power_plug.GND, Diode.anode, Transistor.source, R1.leg2
  N3: 5V_Voltage_Regulator.output_voltage, R1.leg1
  N4: Transistor.gate, R1.wiper
