# Fritzing sketch Electricity lab parallel (saved by Fritzing 0.6.2b)
breadboards: 1

parts:
  Voltage_Regulator = Voltage Regulator - 5V [package="TO220 [THT]"]
  LED1 = Red LED - 5mm
  560_ohm = Resistor [resistance=560 tolerance=±5% package=THT]
  S1 = Pushbutton [package="[THT]"]
  LED2 = Red LED - 5mm
  LED3 = Red LED - 5mm [package="5 mm [THT]"]

nets:
  N1: Voltage_Regulator.GND, LED1.cathode, LED2.cathode, LED3.cathode
  N2: Voltage_Regulator.output_voltage, S1.Pin_3, S1.Pin_4
  N3: LED1.anode, 560_ohm.Pin_0, LED2.anode, LED3.anode
  N4: 560_ohm.Pin_1, S1.Pin_1, S1.Pin_2
