# Fritzing sketch SerialLab2 (saved by Fritzing 0.6.3b)
breadboards: 1

parts:
  Arduino2 = Arduino Uno
  S1 = Round Pushbutton
  R1 = Resistor [tolerance=±5% resistance=10k package=THT]
  U1 = 3-Axis Accelerometer Breakout

nets:
  N1: Arduino2.connector1, Arduino2.connector19, R1.Pin_0, U1.GND
  N2: Arduino2.connector13, S1.leg1, R1.Pin_1
  N3: Arduino2.connector18, S1.leg0, U1.VDD
  GND: Arduino2.connector20
  N4: Arduino2.connector22, U1.Y
  N5: Arduino2.connector23, U1.X
